// Logisim project Cosas que faltan.circ as structural Verilog
module Waiter (
  input  in_1,
  input  in_2,
  input  [3:0] in_3,
  input  [3:0] in_4
);

  wire Aux___Wait_Time, Clk, demultiplexer_1_out0, demultiplexer_1_out1, demultiplexer_2_out0,
       demultiplexer_3_out0, demultiplexer_3_out1, End_q, IDLE_q, Load_aux__1, or_1_out, or_2_out, Reset,
       wait_time_finished, While_q;
  wire [3:0] Aux___1, Aux_Value, Wait_Time;

  Clock clock_1 (.out(Clk));
  not not_1 (Reset, in_1);
  D_Flip_Flop IDLE (.clk(Clk), .D(or_1_out), .Q(IDLE_q), .preset(Reset));  // open: Qn, en, reset
  or or_1 (or_1_out, demultiplexer_1_out0, demultiplexer_3_out1);
  Demultiplexer #(.enable("false")) demultiplexer_1 (
    .out0(demultiplexer_1_out0), .out1(demultiplexer_1_out1), .in(IDLE_q), .sel(in_1));
  Register #(.width(4)) register_1 (.D(Aux___1), .en(Load_aux__1), .Q(Aux_Value), .clk(Clk), .clr(Reset));
  // Probe on Aux_Value
  Adder #(.width(4)) adder_1 (.a(Aux_Value), .b(4'b0001), .out(Aux___1));  // open: cin, cout
  Multiplexer #(.width(4), .enable("false")) multiplexer_1 (.in0(in_3), .in1(in_4), .out(Wait_Time), .sel(in_2));
  Demultiplexer #(.enable("false")) demultiplexer_2 (
    .out0(demultiplexer_2_out0), .out1(Load_aux__1), .in(or_2_out), .sel(Aux___Wait_Time));
  or or_2 (or_2_out, demultiplexer_1_out1, While_q);
  or or_3 (wait_time_finished, demultiplexer_3_out0, demultiplexer_2_out0);
  Comparator #(.width(4), .mode("unsigned")) comparator_1 (
    .a(Aux_Value), .b(Wait_Time), .lt(Aux___Wait_Time));  // open: gt, eq
  D_Flip_Flop End (.clk(Clk), .D(wait_time_finished), .Q(End_q));  // open: Qn, preset, en, reset
  D_Flip_Flop While (.clk(Clk), .D(Load_aux__1), .Q(While_q));  // open: Qn, preset, en, reset
  Demultiplexer #(.enable("false")) demultiplexer_3 (
    .out0(demultiplexer_3_out0), .out1(demultiplexer_3_out1), .in(End_q), .sel(Reset));

  // Other names for the same wires on the sheet: R_W = in_2; Read_Time[3:0] = in_3; Start = in_1;
  //   Write_Time[3:0] = in_4
endmodule

module Little_Endian (
  input  [31:0] Input,
  output [31:0] out_2
);


  assign out_2 = {Input[7:0], Input[15:8], Input[23:16], Input[31:24]};

  // Other names for the same wires on the sheet: d[7:0] = Input[31:24]; c[7:0] = Input[23:16]; b[7:0] = Input[15:8];
  //   a[7:0] = Input[7:0]

  // Notes on the sheet:
  //   Little Endian
endmodule

module RAM_Reader (
  input  [31:0] RAM_Input_1,
  input  [31:0] RAM_Input_2,
  input  [31:0] RAM_Input_3,
  input  [31:0] RAM_Input_4,
  input  [1:0] offset,
  output [31:0] RAM_Input_Selected
);

  wire [31:0] multiplexer_1_out;

  Multiplexer #(.select(2), .width(32), .enable("false")) multiplexer_1 (
    .in0(RAM_Input_1), .in1(RAM_Input_2), .in2(RAM_Input_3), .in3(RAM_Input_4), .out(multiplexer_1_out),
    .sel(offset));
  Little_Endian little_endian_1 (.Input(multiplexer_1_out), .out_2(RAM_Input_Selected));

  // Notes on the sheet:
  //   RAM Reader
endmodule

module RAM_Writer (
  input  [31:0] Input,
  input  [1:0] offset,
  output [31:0] Output,
  output [31:0] Output_2,
  output [31:0] Output_3,
  output [31:0] Output_4,
  output [3:0] Mask
);

  wire [31:0] little_endian_1_out_2;

  Little_Endian little_endian_1 (.Input(Input), .out_2(little_endian_1_out_2));
  Demultiplexer #(.select(2), .width(32), .enable("false")) demultiplexer_1 (
    .out0(Output), .out1(Output_2), .out2(Output_3), .out3(Output_4), .in(little_endian_1_out_2), .sel(offset));
  Multiplexer #(.select(2), .width(4), .enable("false")) multiplexer_1 (
    .in0(4'b0001), .in1(4'b0010), .in2(4'b0100), .in3(4'b1000), .out(Mask), .sel(offset));

  // Notes on the sheet:
  //   RAM Writer
endmodule
