// Logisim project ale_s-mips.circ as structural Verilog
module S_MIPS_Board (
  input  DESHABILITAR_DISPATCHER,
  output halt
);

  wire button_1_out, CLK, CS, d_ff_1_q, LCLR, LoadRAM, LoadRAMOn, LW, R_R_W, R_W, ram_dispatcher_1_finished,
       RCS, Reset_out, RST, TTY_EN;
  wire [2:0] KDB;
  wire [3:0] LMask, Mask, ram_1_read_time, ram_1_write_time, RMask;
  wire [6:0] KDB_DATA, TTY_DATA;
  wire [15:0] Addr, LAddr, RAddr;
  wire [31:0] I0, I1, I2, I3, LData, ram_1_data_out_0, ram_1_data_out_1, ram_1_data_out_2, ram_1_data_out_3,
       RI0, RI1, RI2, RI3;

  TTY #(.rows(25), .cols(80)) tty_1 (.data(TTY_DATA), .clk(CLK), .we(TTY_EN), .clr(RST));
  not not_1 (LoadRAMOn, ram_dispatcher_1_finished);
  RAM_Dispatcher ram_dispatcher_1 (
    .WriteTime(ram_1_write_time), .Clock(CLK), .Data(LData), .Address(LAddr), .Mask(LMask),
    .Finished(ram_dispatcher_1_finished), .Write(LW), .CLR(LCLR));
  Keyboard #(.buflen(64)) keyboard_1 (.clk(CLK), .re(KDB[0]), .avail(KDB[2]), .data(KDB_DATA));  // open: clr
  RAM ram_1 (
    .Address(RAddr), .Data_Out_0(ram_1_data_out_0), .Data_Out_1(ram_1_data_out_1),
    .Data_Out_2(ram_1_data_out_2), .Data_Out_3(ram_1_data_out_3), .Data_In_0(RI0), .Data_In_1(RI1),
    .Data_In_2(RI2), .Data_In_3(RI3), .Mask(RMask), .nRead_Write(R_R_W), .Chip_Select(RCS),
    .Read_Time(ram_1_read_time), .Reset(button_1_out), .Write_Time(ram_1_write_time));
  Button button_1 (.out(button_1_out));
  D_Flip_Flop d_ff_1 (.clk(CLK), .D(1'b1), .Q(d_ff_1_q), .reset(Reset_out));  // open: Qn, preset, en
  Button Reset (.out(Reset_out));
  S_MIPS s_mips_1 (
    .Kbd_Enable(KDB[0]), .Address(Addr), .Kbd_Clear(KDB[1]), .Kbd_Available(KDB[2]), .RAM_In_0(I0),
    .Kbd_ASCII_Data(KDB_DATA), .RAM_In_1(I1), .TTY_Enable(TTY_EN), .RAM_In_2(I2), .RAM_In_3(I3),
    .TTY_ASCII_Data(TTY_DATA), .Reset(RST), .RAM_Out_0(ram_1_data_out_0), .Clock(CLK),
    .RAM_Out_1(ram_1_data_out_1), .Stop(halt), .RAM_Out_2(ram_1_data_out_2), .RAM_Out_3(ram_1_data_out_3),
    .Mask(Mask), .Read_Time(ram_1_read_time), .Write_Time(ram_1_write_time), .nRead_Write(R_W),
    .Chip_Select(CS));
  D_Flip_Flop d_ff_2 (.clk(CLK), .D(d_ff_1_q), .Qn(LCLR), .reset(Reset_out));  // open: Q, preset, en
  or or_1 (RST, LCLR, LoadRAM);
  Clock clock_1 (.out(CLK));
  Multiplexer #(.width(32), .enable("false")) multiplexer_1 (.in0(I0), .in1(LData), .out(RI0), .sel(LoadRAM));
  Multiplexer #(.width(32), .enable("false")) multiplexer_2 (.in0(I1), .in1(LData), .out(RI1), .sel(LoadRAM));
  Multiplexer #(.width(32), .enable("false")) multiplexer_3 (.in0(I2), .in1(LData), .out(RI2), .sel(LoadRAM));
  Multiplexer #(.width(32), .enable("false")) multiplexer_4 (.in0(I3), .in1(LData), .out(RI3), .sel(LoadRAM));
  and and_1 (LoadRAM, ~DESHABILITAR_DISPATCHER, LoadRAMOn);  // AND_Gate
  Multiplexer #(.width(16), .enable("false")) multiplexer_5 (.in0(Addr), .in1(LAddr), .out(RAddr), .sel(LoadRAM));
  Multiplexer #(.width(4), .enable("false")) multiplexer_6 (.in0(Mask), .in1(LMask), .out(RMask), .sel(LoadRAM));
  Multiplexer #(.enable("false")) multiplexer_7 (.in0(CS), .in1(LW), .out(RCS), .sel(LoadRAM));
  Multiplexer #(.enable("false")) multiplexer_8 (.in0(R_W), .in1(LW), .out(R_R_W), .sel(LoadRAM));

  // Notes on the sheet:
  //   NO MODIFICAR
  //   Keyboard
endmodule

module RAM (
  input  [15:0] Address,
  input  [31:0] Data_In_0,
  input  [31:0] Data_In_1,
  input  [31:0] Data_In_2,
  input  [31:0] Data_In_3,
  input  [3:0] Mask,
  input  nRead_Write,
  input  Chip_Select,
  input  Reset,
  output [31:0] Data_Out_0,
  output [31:0] Data_Out_1,
  output [31:0] Data_Out_2,
  output [31:0] Data_Out_3,
  output [3:0] Read_Time,
  output [3:0] Write_Time
);

  wire and_2_out, and_3_out, and_4_out, and_5_out, and_6_out, and_7_out, and_8_out, and_9_out, Changed, CLK,
       comparator_2_eq, comparator_3_eq, comparator_4_eq, comparator_5_eq, comparator_6_eq, Count,
       demultiplexer_3_out0, Idle, Idle_q, Load, Load0, Load1, nand_1_out, or_1_out, or_2_out, or_3_out,
       or_4_out, or_5_out, or_6_out, or_7_out, or_8_out, or_9_out, or_10_out, Proc_q, Update_Mem, Zero_Time;
  wire [3:0] counter_1_q, multiplexer_1_out, subtractor_1_out;
  wire [31:0] register_1_q, register_2_q, register_3_q, register_4_q, register_5_q;

  // Probe on 4'b0011
  // Probe on 4'b0010
  Multiplexer #(.width(4), .enable("false")) multiplexer_1 (
    .in0(4'b0011), .in1(4'b0010), .out(multiplexer_1_out), .sel(nRead_Write));
  or or_1 (or_1_out, Idle, Update_Mem);
  or or_2 (or_2_out, ~Chip_Select, Reset);  // OR_Gate
  Subtractor #(.width(4)) subtractor_1 (.a(multiplexer_1_out), .b(4'b0010), .out(subtractor_1_out));  // open: bin, bout
  Demultiplexer #(.enable("false")) demultiplexer_1 (.out0(Idle), .out1(Load0), .in(Idle_q), .sel(Changed));
  D_Flip_Flop u_Idle (.clk(CLK), .D(or_1_out), .Q(Idle_q), .preset(or_2_out));  // open: Qn, en, reset
  // Probe on counter_1_q
  Counter #(.width(4), .max('hf)) counter_1 (
    .load(Load), .D(subtractor_1_out), .count(Count), .Q(counter_1_q), .clk(CLK), .clr(or_3_out));  // open: carry
  or or_3 (or_3_out, ~Chip_Select, Reset);  // OR_Gate
  Comparator #(.width(4), .mode("unsigned")) comparator_1 (
    .a(4'b0000), .b(counter_1_q), .eq(Zero_Time));  // open: gt, lt
  or or_4 (or_4_out, Count, Load0, Load1);
  Register #(.width(32)) register_1 (.D(Data_In_0), .en(Chip_Select), .Q(register_1_q), .clk(CLK), .clr(or_5_out));
  or or_5 (or_5_out, ~Chip_Select, Reset);  // OR_Gate
  Register #(.width(32)) register_2 (.D(Data_In_1), .en(Chip_Select), .Q(register_2_q), .clk(CLK), .clr(or_6_out));
  or or_6 (or_6_out, ~Chip_Select, Reset);  // OR_Gate
  Register #(.width(32)) register_3 (.D(Data_In_2), .en(Chip_Select), .Q(register_3_q), .clk(CLK), .clr(or_7_out));
  or or_7 (or_7_out, ~Chip_Select, Reset);  // OR_Gate
  Register #(.width(32)) register_4 (.D(Data_In_3), .en(Chip_Select), .Q(register_4_q), .clk(CLK), .clr(or_8_out));
  or or_8 (or_8_out, ~Chip_Select, Reset);  // OR_Gate
  Register #(.width(32)) register_5 (
    .D({{11{1'b1}}, nRead_Write, Mask, Address}), .en(Chip_Select), .Q(register_5_q), .clk(CLK),
    .clr(or_9_out));
  or or_9 (or_9_out, ~Chip_Select, Reset);  // OR_Gate
  D_Flip_Flop Proc (.clk(CLK), .D(or_4_out), .Q(Proc_q), .reset(or_10_out));  // open: Qn, preset, en
  or or_10 (or_10_out, ~Chip_Select, Reset);  // OR_Gate
  Demultiplexer #(.enable("false")) demultiplexer_2 (
    .out0(Count), .out1(Update_Mem), .in(demultiplexer_3_out0), .sel(Zero_Time));
  Demultiplexer #(.enable("false")) demultiplexer_3 (
    .out0(demultiplexer_3_out0), .out1(Load1), .in(Proc_q), .sel(Changed));
  Clock clock_1 (.out(CLK));
  Comparator #(.width(32)) comparator_2 (.a(register_1_q), .b(Data_In_0), .eq(comparator_2_eq));  // open: gt, lt
  Comparator #(.width(32)) comparator_3 (.a(register_2_q), .b(Data_In_1), .eq(comparator_3_eq));  // open: gt, lt
  Comparator #(.width(32)) comparator_4 (.a(register_3_q), .b(Data_In_2), .eq(comparator_4_eq));  // open: gt, lt
  Comparator #(.width(32)) comparator_5 (.a(register_4_q), .b(Data_In_3), .eq(comparator_5_eq));  // open: gt, lt
  Comparator #(.width(32)) comparator_6 (
    .a(register_5_q), .b({{11{1'b1}}, nRead_Write, Mask, Address}), .eq(comparator_6_eq));  // open: gt, lt
  nand nand_1 (nand_1_out, comparator_6_eq, comparator_2_eq, comparator_3_eq, comparator_4_eq, comparator_5_eq);
  and and_1 (Changed, nand_1_out, Chip_Select);
  or or_11 (Load, Count, Load1, Load0);
  and and_2 (and_2_out, Mask[0], Update_Mem, nRead_Write);
  and and_3 (and_3_out, Mask[1], Update_Mem, nRead_Write);
  and and_4 (and_4_out, Mask[2], Update_Mem, nRead_Write);
  and and_5 (and_5_out, Mask[3], Update_Mem, nRead_Write);
  RAM_part #(.addrWidth(16), .dataWidth(32), .bus("separate")) ram_1 (
    .addr(Address), .din(Data_In_0), .data(Data_Out_0), .str(and_2_out), .sel(Chip_Select), .clk(CLK),
    .ld(and_6_out), .clr(Reset));
  and and_6 (and_6_out, ~nRead_Write, Idle);  // AND_Gate
  RAM_part #(.addrWidth(16), .dataWidth(32), .bus("separate")) ram_2 (
    .addr(Address), .din(Data_In_1), .data(Data_Out_1), .str(and_3_out), .sel(Chip_Select), .clk(CLK),
    .ld(and_7_out), .clr(Reset));
  and and_7 (and_7_out, ~nRead_Write, Idle);  // AND_Gate
  RAM_part #(.addrWidth(16), .dataWidth(32), .bus("separate")) ram_3 (
    .addr(Address), .din(Data_In_2), .data(Data_Out_2), .str(and_4_out), .sel(Chip_Select), .clk(CLK),
    .ld(and_8_out), .clr(Reset));
  and and_8 (and_8_out, ~nRead_Write, Idle);  // AND_Gate
  RAM_part #(.addrWidth(16), .dataWidth(32), .bus("separate")) ram_4 (
    .addr(Address), .din(Data_In_3), .data(Data_Out_3), .str(and_5_out), .sel(Chip_Select), .clk(CLK),
    .ld(and_9_out), .clr(Reset));
  and and_9 (and_9_out, ~nRead_Write, Idle);  // AND_Gate

  assign Read_Time = 4'b0011;
  assign Write_Time = 4'b0010;

  // Other names for the same wires on the sheet: M0 = Mask[0]; M1 = Mask[1]; M2 = Mask[2]; M3 = Mask[3];
  //   RW = nRead_Write; CLR = Reset; CS = Chip_Select; Load2 = Count

  // Notes on the sheet:
  //   NO MODIFICAR
  //   excepto quizás los valores RT y WT
  //   BANK0
  //   BANK1
  //   BANK2
  //   BANK3
endmodule

module S_MIPS (
  input  Kbd_Available,
  input  [6:0] Kbd_ASCII_Data,
  input  [31:0] RAM_Out_0,
  input  [31:0] RAM_Out_1,
  input  Reset,
  input  [31:0] RAM_Out_2,
  input  Clock,
  input  [31:0] RAM_Out_3,
  input  [3:0] Read_Time,
  input  [3:0] Write_Time,
  output Kbd_Enable,
  output [15:0] Address,
  output Kbd_Clear,
  output TTY_Enable,
  output [6:0] TTY_ASCII_Data,
  output Stop,
  output [31:0] RAM_In_0,
  output [31:0] RAM_In_1,
  output [31:0] RAM_In_2,
  output [31:0] RAM_In_3,
  output [3:0] Mask,
  output nRead_Write,
  output Chip_Select
);


  // Other names for the same wires on the sheet: CLK = Clock; CLR = Reset; CS = Chip_Select;
  //   KBD_AVAIL = Kbd_Available; KBD_CLR = Kbd_Clear; KBD_DATA[6:0] = Kbd_ASCII_Data; RAM_A[15:0] = Address;
  //   RAM_INPUT_0[31:0] = RAM_In_0; RAM_INPUT_1[31:0] = RAM_In_1; RAM_INPUT_2[31:0] = RAM_In_2;
  //   RAM_INPUT_3[31:0] = RAM_In_3; RAM_MASK[3:0] = Mask; RAM_OUTPUT_0[31:0] = RAM_Out_0;
  //   RAM_OUTPUT_1[31:0] = RAM_Out_1; RAM_OUTPUT_2[31:0] = RAM_Out_2; RAM_OUTPUT_3[31:0] = RAM_Out_3;
  //   RW = nRead_Write; TTY_DATA[6:0] = TTY_ASCII_Data

  // Notes on the sheet:
  //   RAM ADDRESS
  //   DATA FROM RAM
  //   DATA TO RAM
  //   DATA WRITE MASK
  //   RAM TIMING
  //   RAM CONTROL
  //   KEYBOARD
  //   TTY
  //   SEQUENCING
endmodule

module RAM_Dispatcher (
  input  [3:0] WriteTime,
  input  Clock,
  input  CLR,
  output [31:0] Data,
  output [15:0] Address,
  output [3:0] Mask,
  output Finished,
  output Write
);

  wire demultiplexer_2_out1, demultiplexer_3_out1, End, IDLE_q, IncAddr, Load, or_1_out, or_2_out, While_q,
       WriteEnd;
  wire [3:0] counter_1_q;
  wire [31:0] CurrentAddress_q;

  Counter #(.width(32), .max('hffffffff)) CurrentAddress (
    .count(IncAddr), .Q({CurrentAddress_q[31:18], Address, CurrentAddress_q[1:0]}), .clk(Clock), .clr(CLR));  // open: load, D, carry
  or or_1 (or_1_out, IncAddr, demultiplexer_3_out1, Finished);
  D_Flip_Flop IDLE (.clk(Clock), .D(or_1_out), .Q(IDLE_q), .preset(CLR));  // open: Qn, en, reset
  Demultiplexer #(.enable("false")) demultiplexer_1 (.out0(Load), .out1(Finished), .in(IDLE_q), .sel(End));
  D_Flip_Flop While (.clk(Clock), .D(or_2_out), .Q(While_q), .reset(CLR));  // open: Qn, preset, en
  or or_2 (or_2_out, Write, Load);
  RAM_part #(.addrWidth(18), .dataWidth(32)) ram_1 (
    .addr({Address, CurrentAddress_q[1:0]}), .data(Data), .clk(Clock));  // open: sel, ld, clr
  Demultiplexer #(.enable("false")) demultiplexer_2 (
    .out0(Write), .out1(demultiplexer_2_out1), .in(While_q), .sel(WriteEnd));
  Decoder #(.select(2)) decoder_1 (
    .out0(Mask[0]), .out1(Mask[1]), .out2(Mask[2]), .out3(Mask[3]), .sel(CurrentAddress_q[1:0]));  // open: en
  Demultiplexer #(.enable("false")) demultiplexer_3 (
    .out0(IncAddr), .out1(demultiplexer_3_out1), .in(demultiplexer_2_out1), .sel(End));
  Counter #(.width(4), .max('hf)) counter_1 (
    .load(Load), .D(WriteTime), .count(Write), .Q(counter_1_q), .clk(Clock));  // open: carry, clr
  Comparator #(.width(32)) comparator_1 (.a(Data), .b({32{1'b1}}), .eq(End));  // open: gt, lt
  Comparator #(.width(4)) comparator_2 (.a(4'b0000), .b(counter_1_q), .eq(WriteEnd));  // open: gt, lt

  // Other names for the same wires on the sheet: CLK = Clock; Count = Write; WT[3:0] = WriteTime
endmodule

module Data_Path (
);

  wire [31:0] A, B, F, multiplexer_1_out;

  Instruction_Decoder instruction_decoder_1 ();  // open: Input_from_the_RAM, nop, add, sub, mult, mulu, div, divu, slt, sltu, and, or, nor, xor, addi, slti, sltiu, andi, ori, xori, lw, sw, pop, push, beq, bne, blez, bgtz, bltz, j, jr, mfhi, mflo, halt, tty, rnd, kbd, func_code, Rd, Rt, Rs, op_code, op_code_2, op_code_3
  Branch_Control branch_control_1 ();
  Register_File register_file_1 (
    .Output_A(A), .Output_B(B));  // open: Data_address, Data_input, Read_Write, Reset, Clock, Selector_A, Selector_B
  Multiplexer #(.width(32)) multiplexer_1 (.in0(B), .out(multiplexer_1_out));  // open: in1, sel, en
  ALU alu_1 (.A(multiplexer_1_out), .B(A), .Output(F));  // open: LO, HI, OP
endmodule

module Register_File (
  input  [31:0] Data_input,
  input  [4:0] Data_address,
  input  Read_Write,
  input  Reset,
  input  Clock,
  input  [4:0] Selector_A,
  input  [4:0] Selector_B,
  output [31:0] Output_A,
  output [31:0] Output_B
);

  wire e0, e1, e2, e3, e4, e5, e6, e7, e8, e9, e10, e11, e12, e13, e14, e15, e16, e17, e18, e19, e20, e21,
       e22, e23, e24, e25, e26, e27, e28, e29, e30, e31;
  wire [31:0] S0, S1, S2, S3, S4, S5, S6, S7, S8, S9, S10, S11, S12, S13, S14, S15, S16, S17, S18, S19, S20,
       S21, S22, S23, S24, S25, S26, S27, S28, S29, S30, S31;

  Register #(.width(32)) R31 (.D(Data_input), .en(e31), .Q(S31), .clk(Clock), .clr(Reset));
  Register #(.width(32)) R23 (.D(Data_input), .en(e23), .Q(S23), .clk(Clock), .clr(Reset));
  Register #(.width(32)) R15 (.D(Data_input), .en(e15), .Q(S15), .clk(Clock), .clr(Reset));
  Register #(.width(32)) R7 (.D(Data_input), .en(e7), .Q(S7), .clk(Clock), .clr(Reset));
  Register #(.width(32)) R30 (.D(Data_input), .en(e30), .Q(S30), .clk(Clock), .clr(Reset));
  Register #(.width(32)) R22 (.D(Data_input), .en(e22), .Q(S22), .clk(Clock), .clr(Reset));
  Register #(.width(32)) R14 (.D(Data_input), .en(e14), .Q(S14), .clk(Clock), .clr(Reset));
  Register #(.width(32)) R6 (.D(Data_input), .en(e6), .Q(S6), .clk(Clock), .clr(Reset));
  Register #(.width(32)) R29 (.D(Data_input), .en(e29), .Q(S29), .clk(Clock), .clr(Reset));
  Register #(.width(32)) R21 (.D(Data_input), .en(e21), .Q(S21), .clk(Clock), .clr(Reset));
  Register #(.width(32)) R13 (.D(Data_input), .en(e13), .Q(S13), .clk(Clock), .clr(Reset));
  Register #(.width(32)) R5 (.D(Data_input), .en(e5), .Q(S5), .clk(Clock), .clr(Reset));
  Register #(.width(32)) R28 (.D(Data_input), .en(e28), .Q(S28), .clk(Clock), .clr(Reset));
  Register #(.width(32)) R20 (.D(Data_input), .en(e20), .Q(S20), .clk(Clock), .clr(Reset));
  Register #(.width(32)) R12 (.D(Data_input), .en(e12), .Q(S12), .clk(Clock), .clr(Reset));
  Register #(.width(32)) R4 (.D(Data_input), .en(e4), .Q(S4), .clk(Clock), .clr(Reset));
  Register #(.width(32)) R27 (.D(Data_input), .en(e27), .Q(S27), .clk(Clock), .clr(Reset));
  Register #(.width(32)) R19 (.D(Data_input), .en(e19), .Q(S19), .clk(Clock), .clr(Reset));
  Register #(.width(32)) R11 (.D(Data_input), .en(e11), .Q(S11), .clk(Clock), .clr(Reset));
  Register #(.width(32)) R3 (.D(Data_input), .en(e3), .Q(S3), .clk(Clock), .clr(Reset));
  Demultiplexer #(.select(5)) demultiplexer_1 (
    .out0(e0), .out1(e1), .out2(e2), .out3(e3), .out4(e4), .out5(e5), .out6(e6), .out7(e7), .out8(e8),
    .out9(e9), .out10(e10), .out11(e11), .out12(e12), .out13(e13), .out14(e14), .out15(e15), .out16(e16),
    .out17(e17), .out18(e18), .out19(e19), .out20(e20), .out21(e21), .out22(e22), .out23(e23), .out24(e24),
    .out25(e25), .out26(e26), .out27(e27), .out28(e28), .out29(e29), .out30(e30), .out31(e31),
    .in(Read_Write), .sel(Data_address));  // open: en
  Register #(.width(32)) R26 (.D(Data_input), .en(e26), .Q(S26), .clk(Clock), .clr(Reset));
  Register #(.width(32)) R18 (.D(Data_input), .en(e18), .Q(S18), .clk(Clock), .clr(Reset));
  Register #(.width(32)) R10 (.D(Data_input), .en(e10), .Q(S10), .clk(Clock), .clr(Reset));
  Register #(.width(32)) R2 (.D(Data_input), .en(e2), .Q(S2), .clk(Clock), .clr(Reset));
  Register #(.width(32)) R25 (.D(Data_input), .en(e25), .Q(S25), .clk(Clock), .clr(Reset));
  Register #(.width(32)) R17 (.D(Data_input), .en(e17), .Q(S17), .clk(Clock), .clr(Reset));
  Register #(.width(32)) R9 (.D(Data_input), .en(e9), .Q(S9), .clk(Clock), .clr(Reset));
  Register #(.width(32)) R1 (.D(Data_input), .en(e1), .Q(S1), .clk(Clock), .clr(Reset));
  Register #(.width(32)) R24 (.D(Data_input), .en(e24), .Q(S24), .clk(Clock), .clr(Reset));
  Register #(.width(32)) R16 (.D(Data_input), .en(e16), .Q(S16), .clk(Clock), .clr(Reset));
  Register #(.width(32)) R8 (.D(Data_input), .en(e8), .Q(S8), .clk(Clock), .clr(Reset));
  Register #(.width(32)) R0 (.D({32{1'b0}}), .en(e0), .Q(S0), .clk(Clock), .clr(Reset));
  Multiplexer #(.select(5), .width(32)) multiplexer_1 (
    .in0(S0), .in1(S1), .in2(S2), .in3(S3), .in4(S4), .in5(S5), .in6(S6), .in7(S7), .in8(S8), .in9(S9),
    .in10(S10), .in11(S11), .in12(S12), .in13(S13), .in14(S14), .in15(S15), .in16(S16), .in17(S17),
    .in18(S18), .in19(S19), .in20(S20), .in21(S21), .in22(S22), .in23(S23), .in24(S24), .in25(S25),
    .in26(S26), .in27(S27), .in28(S28), .in29(S29), .in30(S30), .in31(S31), .out(Output_A), .sel(Selector_A));  // open: en
  Multiplexer #(.select(5), .width(32)) multiplexer_2 (
    .in0(S0), .in1(S1), .in2(S2), .in3(S3), .in4(S4), .in5(S5), .in6(S6), .in7(S7), .in8(S8), .in9(S9),
    .in10(S10), .in11(S11), .in12(S12), .in13(S13), .in14(S14), .in15(S15), .in16(S16), .in17(S17),
    .in18(S18), .in19(S19), .in20(S20), .in21(S21), .in22(S22), .in23(S23), .in24(S24), .in25(S25),
    .in26(S26), .in27(S27), .in28(S28), .in29(S29), .in30(S30), .in31(S31), .out(Output_B), .sel(Selector_B));  // open: en

  // Other names for the same wires on the sheet: A[31:0] = Output_A; B[31:0] = Output_B; c = Clock;
  //   D[31:0] = Data_input; DA[4:0] = Data_address; Rst = Reset; rw = Read_Write; SA[4:0] = Selector_A;
  //   SB[4:0] = Selector_B

  // Notes on the sheet:
  //   Registros
  //   Enables
  //   Salidas
  //   Selectores de salida
endmodule

module ALU (
  input  [31:0] A,
  input  [31:0] B,
  input  [5:0] OP,
  output [31:0] Output,
  output [31:0] LO,
  output [31:0] HI
);

  wire com, comparator_1_lt, comparator_2_lt, u;
  wire [31:0] \and , div_hi, div_lo, divu_hi, divu_lo, mul_hi, mul_lo, mulu_hi, mulu_lo, \nor , \or , slt,
       sltu, sub, sum, tcmh, tcml, to_positive_1_output, to_positive_2_output, to_positive_3_output,
       to_positive_4_output, tuh, tul, \xor ;

  // Probe on Output
  Multiplexer #(.width(4)) multiplexer_1 ();  // open: in0, in1, out, sel, en
  not not_1 (com, OP[5]);
  // Probe on A
  // Probe on B
  // Probe on HI
  Adder #(.width(32)) adder_1 (.a(A), .b(B), .out(sum));  // open: cin, cout
  assign \and  = A & B;  // AND_Gate AND, 32 bits wide
  assign \or  = A | B;  // OR_Gate OR, 32 bits wide
  // Probe on LO
  Subtractor #(.width(32)) subtractor_1 (.a(A), .b(B), .out(sub));  // open: bin, bout
  assign \nor  = ~(A | B);  // NOR_Gate NOR, 32 bits wide
  assign \xor  = A ^ B;  // XOR_Gate XOR, 32 bits wide
  to_positive to_positive_1 (.in_1(A), .Output(to_positive_1_output));
  to_positive to_positive_2 (.in_1(B), .Output(to_positive_2_output));
  Multiplier #(.width(32)) multiplier_1 (
    .a(to_positive_1_output), .b(to_positive_2_output), .out(tul), .cout(tuh));  // open: cin
  xor xor_2 (u, B[31], A[31]);
  _2_Complement_64b u_2_complement_64b_1 (.LO(tul), .HI(tuh), .OLO(tcml), .OHI(tcmh));
  Multiplier #(.width(32)) multiplier_2 (.a(A), .b(B), .out(mulu_lo), .cout(mulu_hi));  // open: cin
  Comparator #(.width(32)) comparator_1 (.a(A), .b(B), .lt(comparator_1_lt));  // open: gt, eq
  Multiplexer #(.width(32)) multiplexer_2 (.in0(tul), .in1(tcml), .out(mul_lo), .sel(u));  // open: en
  Multiplexer #(.width(32)) multiplexer_3 (.in0(tuh), .in1(tcmh), .out(mul_hi), .sel(u));  // open: en
  Multiplexer #(.width(32)) multiplexer_4 (
    .in0({32{1'b0}}), .in1(32'h1), .out(slt), .sel(comparator_1_lt));  // open: en
  Divider #(.width(32)) divider_1 (.a(A), .b(B), .out(div_lo), .rem(div_hi));  // open: upper
  to_positive to_positive_3 (.in_1(A), .Output(to_positive_3_output));
  Divider #(.width(32)) divider_2 (
    .a(to_positive_3_output), .b(to_positive_4_output), .out(divu_lo), .rem(divu_hi));  // open: upper
  to_positive to_positive_4 (.in_1(B), .Output(to_positive_4_output));
  Comparator #(.width(32), .mode("unsigned")) comparator_2 (.a(A), .b(B), .lt(comparator_2_lt));  // open: gt, eq
  Multiplexer #(.width(32)) multiplexer_5 (
    .in0({32{1'b0}}), .in1(32'h1), .out(sltu), .sel(comparator_2_lt));  // open: en
  Multiplexer #(.select(4), .width(32)) multiplexer_6 (
    .in0(sum), .in2(sub), .in4(\and ), .in5(\or ), .in7(\nor ), .in8(\xor ), .in10(slt), .in11(sltu),
    .out(Output), .sel(OP[3:0]));  // open: in1, in3, in6, in9, in12, in13, in14, in15, en
  Multiplexer #(.select(2), .width(32)) multiplexer_7 (
    .in0(mul_lo), .in1(mulu_lo), .in2(div_lo), .in3(divu_lo), .out(LO), .sel(OP[1:0]), .en(com));
  Multiplexer #(.select(2), .width(32)) multiplexer_8 (
    .in0(mul_hi), .in1(mulu_hi), .in2(div_hi), .in3(divu_hi), .out(HI), .sel(OP[1:0]), .en(com));
  RAM ram_1 ();  // open: Address, Data_Out_0, Data_Out_1, Data_Out_2, Data_Out_3, Data_In_0, Data_In_1, Data_In_2, Data_In_3, Mask, nRead_Write, Chip_Select, Read_Time, Reset, Write_Time

  // Other names for the same wires on the sheet: minus_a = A[31]; minus_b = B[31]; op2[1:0] = OP[1:0];
  //   ops[3:0] = OP[3:0]; vlh[31:0] = HI; vlo[31:0] = LO; vr[31:0] = Output

  // Notes on the sheet:
  //   Suma
  //   Lógicos
  //   Resta
  //   Multiplicación
  //   Multiplicación U
  //   Set last then
  //   División
  //   División U
  //   Set last then U
endmodule

module Instruction_Decoder (
  input  [31:0] Input_from_the_RAM,
  output nop,
  output add,
  output div,
  output \and ,
  output j,
  output jr,
  output sub,
  output divu,
  output \or ,
  output mult,
  output slt,
  output \nor ,
  output mulu,
  output sltu,
  output \xor ,
  output lw,
  output bgtz,
  output sw,
  output bltz,
  output addi,
  output andi,
  output halt,
  output pop,
  output slti,
  output ori,
  output tty,
  output push,
  output blez,
  output sltiu,
  output xori,
  output rnd,
  output beq,
  output mfhi,
  output kbd,
  output bne,
  output mflo,
  output [5:0] func_code,
  output [4:0] Rd,
  output [4:0] Rt,
  output [4:0] Rs,
  output [5:0] op_code,
  output [15:0] op_code_2,
  output [25:0] op_code_3
);

  wire and_2_out, and_3_out, and_4_out, and_5_out, and_11_out, and_12_out, and_19_out, and_20_out,
       and_23_out, and_24_out, and_25_out, aritmetica, aritmetica_nop_jr, decoder_select_2b_1__0,
       decoder_select_2b_1__2, decoder_select_2b_1__3, decoder_select_2b_3__0, decoder_select_2b_4__1,
       decoder_select_2b_5__0, decoder_select_2b_5__2, not_1_out, not_2_out, not_3_out, not_4_out, not_5_out,
       not_6_out, not_7_out, not_8_out, not_9_out, not_10_out, not_11_out, not_12_out, not_13_out,
       not_14_out, not_15_out, not_16_out, not_17_out, not_18_out, not_19_out, not_20_out, not_21_out,
       not_22_out, not_23_out, not_24_out, not_25_out, not_26_out, not_27_out, not_28_out, not_29_out,
       not_30_out, not_31_out, not_32_out, not_33_out, or_1_out;
  wire [2:0] bitselector_1_out, bitselector_2_out;

  not not_1 (not_1_out, Input_from_the_RAM[6]);
  not not_2 (not_2_out, Input_from_the_RAM[7]);
  not not_3 (not_3_out, Input_from_the_RAM[8]);
  not not_4 (not_4_out, Input_from_the_RAM[9]);
  not not_5 (not_5_out, Input_from_the_RAM[10]);
  not not_6 (not_6_out, Input_from_the_RAM[11]);
  not not_7 (not_7_out, Input_from_the_RAM[12]);
  not not_8 (not_8_out, Input_from_the_RAM[13]);
  not not_9 (not_9_out, Input_from_the_RAM[14]);
  not not_10 (not_10_out, Input_from_the_RAM[15]);
  not not_11 (not_11_out, Input_from_the_RAM[16]);
  not not_12 (not_12_out, Input_from_the_RAM[17]);
  not not_13 (not_13_out, Input_from_the_RAM[18]);
  not not_14 (not_14_out, Input_from_the_RAM[19]);
  not not_15 (not_15_out, Input_from_the_RAM[20]);
  not not_16 (not_16_out, Input_from_the_RAM[26]);
  not not_17 (not_17_out, Input_from_the_RAM[27]);
  not not_18 (not_18_out, Input_from_the_RAM[28]);
  not not_19 (not_19_out, Input_from_the_RAM[29]);
  not not_20 (not_20_out, Input_from_the_RAM[30]);
  not not_21 (not_21_out, Input_from_the_RAM[31]);
  and and_1 (aritmetica_nop_jr, ~Input_from_the_RAM[26], ~Input_from_the_RAM[27], ~Input_from_the_RAM[28], ~Input_from_the_RAM[29], ~Input_from_the_RAM[30], ~Input_from_the_RAM[31]);  // AND_Gate
  and and_2 (and_2_out, not_1_out, not_2_out, not_3_out, not_4_out, not_5_out, not_6_out, not_7_out, not_8_out, not_9_out, not_10_out, not_11_out, not_12_out, not_13_out, not_14_out, not_15_out, not_16_out, not_17_out, not_18_out, not_19_out, not_20_out, not_21_out);
  and and_3 (and_3_out, Input_from_the_RAM[5], aritmetica);
  not not_22 (not_22_out, aritmetica_nop_jr);
  not not_23 (not_23_out, Input_from_the_RAM[21]);
  not not_24 (not_24_out, Input_from_the_RAM[22]);
  not not_25 (not_25_out, Input_from_the_RAM[23]);
  not not_26 (not_26_out, Input_from_the_RAM[24]);
  not not_27 (not_27_out, Input_from_the_RAM[25]);
  not not_28 (not_28_out, Input_from_the_RAM[0]);
  not not_29 (not_29_out, Input_from_the_RAM[1]);
  not not_30 (not_30_out, Input_from_the_RAM[2]);
  not not_31 (not_31_out, Input_from_the_RAM[3]);
  not not_32 (not_32_out, Input_from_the_RAM[4]);
  not not_33 (not_33_out, Input_from_the_RAM[5]);
  and and_4 (and_4_out, and_3_out, Input_from_the_RAM[4]);
  and and_5 (and_5_out, and_3_out, ~Input_from_the_RAM[4]);  // AND_Gate
  // AND_Gate and_6 has open pins: in0=not_23_out, in1=not_24_out, in2=not_25_out, in3=not_26_out, in4=not_27_out, in5=not_28_out, in6=not_29_out, in7=not_30_out, in8=not_31_out, in9=not_32_out, in10=not_33_out, out=open
  Decoder_select_2b decoder_select_2b_1 (
    .Enable(and_5_out), .Seleccionador(2'b00), ._0(decoder_select_2b_1__0), ._1(\or ),
    ._2(decoder_select_2b_1__2), ._3(decoder_select_2b_1__3), .\Objeto_de_selección (Input_from_the_RAM[5:0]));
  and and_7 (halt, Input_from_the_RAM[5], not_22_out);
  and and_8 (tty, ~halt, Input_from_the_RAM[0], not_22_out);  // AND_Gate
  and and_9 (rnd, ~halt, Input_from_the_RAM[1], not_22_out);  // AND_Gate
  and and_10 (kbd, ~halt, Input_from_the_RAM[2], not_22_out);  // AND_Gate
  and and_11 (and_11_out, and_4_out, Input_from_the_RAM[3]);
  and and_12 (and_12_out, ~Input_from_the_RAM[3], and_4_out);  // AND_Gate
  Decoder #(.disabled(0)) decoder_1 (.out0(mfhi), .out1(mflo), .sel(Input_from_the_RAM[1]), .en(and_12_out));
  Decoder_select_2b decoder_select_2b_2 (
    .Enable(and_11_out), .Seleccionador(2'b00), ._0(mult), ._1(mulu), ._2(div), ._3(divu),
    .\Objeto_de_selección (Input_from_the_RAM[5:0]));
  Decoder_select_2b decoder_select_2b_3 (
    .Enable(decoder_select_2b_1__0), .Seleccionador(2'b01), ._0(decoder_select_2b_3__0), ._1(\and ),
    ._2(\xor ), .\Objeto_de_selección (Input_from_the_RAM[5:0]));  // open: _3
  and and_13 (slt, Input_from_the_RAM[3], decoder_select_2b_1__2);
  and and_14 (sub, ~Input_from_the_RAM[3], decoder_select_2b_1__2);  // AND_Gate
  and and_15 (sltu, Input_from_the_RAM[3], ~Input_from_the_RAM[2], decoder_select_2b_1__3);  // AND_Gate
  and and_16 (\nor , ~Input_from_the_RAM[3], Input_from_the_RAM[2], decoder_select_2b_1__3);  // AND_Gate
  BitSelector #(.width(6), .group(3)) bitselector_1 (.in(Input_from_the_RAM[5:0]), .out(bitselector_1_out), .sel(1'b1));
  and and_17 (add, Input_from_the_RAM[5], decoder_select_2b_3__0);
  and and_18 (j, ~Input_from_the_RAM[0], Input_from_the_RAM[1], ~Input_from_the_RAM[2], ~Input_from_the_RAM[3], ~Input_from_the_RAM[4], ~Input_from_the_RAM[5]);  // AND_Gate
  and and_19 (and_19_out, bitselector_1_out[0], bitselector_1_out[1], bitselector_1_out[2]);
  and and_20 (and_20_out, ~bitselector_1_out[0], ~bitselector_1_out[1], ~bitselector_1_out[2]);  // AND_Gate
  BitSelector #(.width(6), .group(3)) bitselector_2 (.in(Input_from_the_RAM[5:0]), .out(bitselector_2_out), .sel(1'b1));
  and and_21 (pop, ~Input_from_the_RAM[26], and_19_out);  // AND_Gate
  and and_22 (push, Input_from_the_RAM[26], and_19_out);
  and and_23 (and_23_out, and_20_out, Input_from_the_RAM[2]);
  or or_1 (or_1_out, and_23_out, and_24_out);
  and and_24 (and_24_out, and_20_out, Input_from_the_RAM[0]);
  and and_25 (and_25_out, ~bitselector_2_out[0], ~bitselector_2_out[1], bitselector_2_out[2]);  // AND_Gate
  and and_26 (lw, Input_from_the_RAM[0], ~Input_from_the_RAM[1], ~Input_from_the_RAM[2], ~Input_from_the_RAM[3], Input_from_the_RAM[4], Input_from_the_RAM[5]);  // AND_Gate
  Decoder_select_2b decoder_select_2b_4 (
    .Enable(or_1_out), .Seleccionador(2'b00), ._0(beq), ._1(decoder_select_2b_4__1), ._2(blez), ._3(bgtz),
    .\Objeto_de_selección (Input_from_the_RAM[31:26]));
  Decoder_select_2b decoder_select_2b_5 (
    .Enable(and_25_out), .Seleccionador(2'b00), ._0(decoder_select_2b_5__0), ._1(ori),
    ._2(decoder_select_2b_5__2), ._3(sltiu), .\Objeto_de_selección (Input_from_the_RAM[31:26]));
  and and_27 (sw, Input_from_the_RAM[0], Input_from_the_RAM[2], ~Input_from_the_RAM[3], Input_from_the_RAM[4], Input_from_the_RAM[5]);  // AND_Gate
  and and_28 (bltz, ~Input_from_the_RAM[2], decoder_select_2b_4__1);  // AND_Gate
  and and_29 (bne, Input_from_the_RAM[2], decoder_select_2b_4__1);
  and and_30 (addi, ~Input_from_the_RAM[2], decoder_select_2b_5__0);  // AND_Gate
  and and_31 (andi, Input_from_the_RAM[2], decoder_select_2b_5__0);
  and and_32 (slti, ~Input_from_the_RAM[2], decoder_select_2b_5__2);  // AND_Gate
  and and_33 (xori, Input_from_the_RAM[2], decoder_select_2b_5__2);

  assign func_code = Input_from_the_RAM[5:0];
  assign op_code = Input_from_the_RAM[31:26];
  assign op_code_2 = Input_from_the_RAM[15:0];
  assign op_code_3 = Input_from_the_RAM[25:0];
  assign Rd = Input_from_the_RAM[15:11];
  assign Rs = Input_from_the_RAM[25:21];
  assign Rt = Input_from_the_RAM[20:16];

  // Other names for the same wires on the sheet: Input[31:0] = Input_from_the_RAM; oc0 = Input_from_the_RAM[26];
  //   oc1 = Input_from_the_RAM[27]; oc2 = Input_from_the_RAM[28]; oc3 = Input_from_the_RAM[29];
  //   oc4 = Input_from_the_RAM[30]; oc5 = Input_from_the_RAM[31]; constant[15:0] = Input_from_the_RAM[15:0];
  //   fc0 = Input_from_the_RAM[0]; jump_dest[25:0] = Input_from_the_RAM[25:0]; fc1 = Input_from_the_RAM[1];
  //   fc2 = Input_from_the_RAM[2]; fc3 = Input_from_the_RAM[3]; fc4 = Input_from_the_RAM[4];
  //   fc5 = Input_from_the_RAM[5]; x[4:0] = Input_from_the_RAM[10:6]

  // Notes on the sheet:
  //   Señales
  //   Especiales
  //   Valores
  //   4
  //   2
  //   5
  //   3
  //   0
  //   1
  //   4
  //   2
  //   5
  //   0
  //   3
  //   1
  //   Especiales
  //   mult/div
  //   Aritméticas y jr,mflo/hi
  //   op
  //   Jump
  //   Los b--, pop, push
  //   Los i-constantes
  //   lw,sw
endmodule

module to_positive (
  input  [31:0] in_1,
  output [31:0] Output
);

  wire n;
  wire [31:0] minus_in;

  Negator #(.width(32)) negator_1 (.in(in_1), .out(minus_in));
  Comparator #(.width(32)) comparator_1 (.a(in_1), .b({32{1'b0}}), .lt(n));  // open: gt, eq
  Multiplexer #(.width(32)) multiplexer_1 (.in0(in_1), .in1(minus_in), .out(Output), .sel(n));  // open: en

  // Other names for the same wires on the sheet: in[31:0] = in_1
endmodule

module _2_Complement_64b (
  input  [31:0] LO,
  input  [31:0] HI,
  output [31:0] OLO,
  output [31:0] OHI
);

  wire adder_1_cout;
  wire [31:0] not_1_out, not_2_out;

  // Probe on LO
  // Probe on HI
  Adder #(.width(32)) adder_1 (.a(32'h1), .b(not_1_out), .out(OLO), .cout(adder_1_cout));  // open: cin
  assign not_1_out = ~LO;  // NOT_Gate not_1, 32 bits wide
  Adder #(.width(32)) adder_2 (.a({32{1'b0}}), .b(not_2_out), .out(OHI), .cin(adder_1_cout));  // open: cout
  assign not_2_out = ~HI;  // NOT_Gate not_2, 32 bits wide
  // Probe on OLO
  // Probe on OHI
endmodule

module Decoder_select_2b (
  input  Enable,
  input  [1:0] Seleccionador,
  input  [5:0] \Objeto_de_selección ,
  output _0,
  output _1,
  output _2,
  output _3
);

  wire [1:0] bitselector_1_out;

  Decoder #(.select(2), .disabled(0)) decoder_1 (
    .out0(_0), .out1(_1), .out2(_2), .out3(_3), .sel(bitselector_1_out), .en(Enable));
  BitSelector #(.width(6), .group(2)) bitselector_1 (
    .in(\Objeto_de_selección ), .out(bitselector_1_out), .sel(Seleccionador));
endmodule
