// Logisim project diani_s-mips.circ as structural Verilog
module S_MIPS_Board (
  input  DESHABILITAR_DISPATCHER,
  output halt
);

  wire button_1_out, CLK, CS, d_ff_1_q, LCLR, LoadRAM, LoadRAMOn, LW, R_R_W, R_W, ram_dispatcher_1_finished,
       RCS, Reset_out, RST, TTY_EN;
  wire [2:0] KDB;
  wire [3:0] LMask, Mask, ram_1_read_time, ram_1_write_time, RMask;
  wire [6:0] KDB_DATA, TTY_DATA;
  wire [15:0] Addr, LAddr, RAddr;
  wire [31:0] I0, I1, I2, I3, LData, ram_1_data_out_0, ram_1_data_out_1, ram_1_data_out_2, ram_1_data_out_3,
       RI0, RI1, RI2, RI3;

  TTY #(.rows(25), .cols(80)) tty_1 (.data(TTY_DATA), .clk(CLK), .we(TTY_EN), .clr(RST));
  not not_1 (LoadRAMOn, ram_dispatcher_1_finished);
  RAM_Dispatcher ram_dispatcher_1 (
    .WriteTime(ram_1_write_time), .Clock(CLK), .Data(LData), .Address(LAddr), .Mask(LMask),
    .Finished(ram_dispatcher_1_finished), .Write(LW), .CLR(LCLR));
  Keyboard #(.buflen(64)) keyboard_1 (.clk(CLK), .re(KDB[0]), .avail(KDB[2]), .data(KDB_DATA));  // open: clr
  RAM ram_1 (
    .Address(RAddr), .Data_Out_0(ram_1_data_out_0), .Data_Out_1(ram_1_data_out_1),
    .Data_Out_2(ram_1_data_out_2), .Data_Out_3(ram_1_data_out_3), .Data_In_0(RI0), .Data_In_1(RI1),
    .Data_In_2(RI2), .Data_In_3(RI3), .Mask(RMask), .nRead_Write(R_R_W), .Chip_Select(RCS),
    .Read_Time(ram_1_read_time), .Reset(button_1_out), .Write_Time(ram_1_write_time));
  Button button_1 (.out(button_1_out));
  D_Flip_Flop d_ff_1 (.clk(CLK), .D(1'b1), .Q(d_ff_1_q), .reset(Reset_out));  // open: Qn, preset, en
  Button Reset (.out(Reset_out));
  S_MIPS s_mips_1 (
    .Kbd_Enable(KDB[0]), .Address(Addr), .Kbd_Clear(KDB[1]), .Kbd_Available(KDB[2]), .RAM_In_0(I0),
    .Kbd_ASCII_Data(KDB_DATA), .RAM_In_1(I1), .TTY_Enable(TTY_EN), .RAM_In_2(I2), .RAM_In_3(I3),
    .TTY_ASCII_Data(TTY_DATA), .Reset(RST), .RAM_Out_0(ram_1_data_out_0), .Clock(CLK),
    .RAM_Out_1(ram_1_data_out_1), .Stop(halt), .RAM_Out_2(ram_1_data_out_2), .RAM_Out_3(ram_1_data_out_3),
    .Mask(Mask), .Read_Time(ram_1_read_time), .Write_Time(ram_1_write_time), .nRead_Write(R_W),
    .Chip_Select(CS));
  D_Flip_Flop d_ff_2 (.clk(CLK), .D(d_ff_1_q), .Qn(LCLR), .reset(Reset_out));  // open: Q, preset, en
  or or_1 (RST, LCLR, LoadRAM);
  Clock clock_1 (.out(CLK));
  Multiplexer #(.width(32), .enable("false")) multiplexer_1 (.in0(I0), .in1(LData), .out(RI0), .sel(LoadRAM));
  Multiplexer #(.width(32), .enable("false")) multiplexer_2 (.in0(I1), .in1(LData), .out(RI1), .sel(LoadRAM));
  Multiplexer #(.width(32), .enable("false")) multiplexer_3 (.in0(I2), .in1(LData), .out(RI2), .sel(LoadRAM));
  Multiplexer #(.width(32), .enable("false")) multiplexer_4 (.in0(I3), .in1(LData), .out(RI3), .sel(LoadRAM));
  and and_1 (LoadRAM, ~DESHABILITAR_DISPATCHER, LoadRAMOn);  // AND_Gate
  Multiplexer #(.width(16), .enable("false")) multiplexer_5 (.in0(Addr), .in1(LAddr), .out(RAddr), .sel(LoadRAM));
  Multiplexer #(.width(4), .enable("false")) multiplexer_6 (.in0(Mask), .in1(LMask), .out(RMask), .sel(LoadRAM));
  Multiplexer #(.enable("false")) multiplexer_7 (.in0(CS), .in1(LW), .out(RCS), .sel(LoadRAM));
  Multiplexer #(.enable("false")) multiplexer_8 (.in0(R_W), .in1(LW), .out(R_R_W), .sel(LoadRAM));

  // Notes on the sheet:
  //   NO MODIFICAR
  //   Keyboard
endmodule

module RAM (
  input  [15:0] Address,
  input  [31:0] Data_In_0,
  input  [31:0] Data_In_1,
  input  [31:0] Data_In_2,
  input  [31:0] Data_In_3,
  input  [3:0] Mask,
  input  nRead_Write,
  input  Chip_Select,
  input  Reset,
  output [31:0] Data_Out_0,
  output [31:0] Data_Out_1,
  output [31:0] Data_Out_2,
  output [31:0] Data_Out_3,
  output [3:0] Read_Time,
  output [3:0] Write_Time
);

  wire and_2_out, and_3_out, and_4_out, and_5_out, and_6_out, and_7_out, and_8_out, and_9_out, Changed, CLK,
       comparator_2_eq, comparator_3_eq, comparator_4_eq, comparator_5_eq, comparator_6_eq, Count,
       demultiplexer_3_out0, Idle, Idle_q, Load, Load0, Load1, nand_1_out, or_1_out, or_2_out, or_3_out,
       or_4_out, or_5_out, or_6_out, or_7_out, or_8_out, or_9_out, or_10_out, Proc_q, Update_Mem, Zero_Time;
  wire [3:0] counter_1_q, multiplexer_1_out, subtractor_1_out;
  wire [31:0] register_1_q, register_2_q, register_3_q, register_4_q, register_5_q;

  // Probe on 4'b0011
  // Probe on 4'b0010
  Multiplexer #(.width(4), .enable("false")) multiplexer_1 (
    .in0(4'b0011), .in1(4'b0010), .out(multiplexer_1_out), .sel(nRead_Write));
  or or_1 (or_1_out, Idle, Update_Mem);
  or or_2 (or_2_out, ~Chip_Select, Reset);  // OR_Gate
  Subtractor #(.width(4)) subtractor_1 (.a(multiplexer_1_out), .b(4'b0010), .out(subtractor_1_out));  // open: bin, bout
  D_Flip_Flop u_Idle (.clk(CLK), .D(or_1_out), .Q(Idle_q), .preset(or_2_out));  // open: Qn, en, reset
  Demultiplexer #(.enable("false")) demultiplexer_1 (.out0(Idle), .out1(Load0), .in(Idle_q), .sel(Changed));
  // Probe on counter_1_q
  Counter #(.width(4), .max('hf)) counter_1 (
    .load(Load), .D(subtractor_1_out), .count(Count), .Q(counter_1_q), .clk(CLK), .clr(or_3_out));  // open: carry
  or or_3 (or_3_out, ~Chip_Select, Reset);  // OR_Gate
  Comparator #(.width(4), .mode("unsigned")) comparator_1 (
    .a(4'b0000), .b(counter_1_q), .eq(Zero_Time));  // open: gt, lt
  or or_4 (or_4_out, Count, Load0, Load1);
  Register #(.width(32)) register_1 (.D(Data_In_0), .en(Chip_Select), .Q(register_1_q), .clk(CLK), .clr(or_5_out));
  or or_5 (or_5_out, ~Chip_Select, Reset);  // OR_Gate
  Register #(.width(32)) register_2 (.D(Data_In_1), .en(Chip_Select), .Q(register_2_q), .clk(CLK), .clr(or_6_out));
  or or_6 (or_6_out, ~Chip_Select, Reset);  // OR_Gate
  Register #(.width(32)) register_3 (.D(Data_In_2), .en(Chip_Select), .Q(register_3_q), .clk(CLK), .clr(or_7_out));
  or or_7 (or_7_out, ~Chip_Select, Reset);  // OR_Gate
  Register #(.width(32)) register_4 (.D(Data_In_3), .en(Chip_Select), .Q(register_4_q), .clk(CLK), .clr(or_8_out));
  or or_8 (or_8_out, ~Chip_Select, Reset);  // OR_Gate
  Register #(.width(32)) register_5 (
    .D({{11{1'b1}}, nRead_Write, Mask, Address}), .en(Chip_Select), .Q(register_5_q), .clk(CLK),
    .clr(or_9_out));
  or or_9 (or_9_out, ~Chip_Select, Reset);  // OR_Gate
  D_Flip_Flop Proc (.clk(CLK), .D(or_4_out), .Q(Proc_q), .reset(or_10_out));  // open: Qn, preset, en
  or or_10 (or_10_out, ~Chip_Select, Reset);  // OR_Gate
  Demultiplexer #(.enable("false")) demultiplexer_2 (
    .out0(Count), .out1(Update_Mem), .in(demultiplexer_3_out0), .sel(Zero_Time));
  Demultiplexer #(.enable("false")) demultiplexer_3 (
    .out0(demultiplexer_3_out0), .out1(Load1), .in(Proc_q), .sel(Changed));
  Clock clock_1 (.out(CLK));
  Comparator #(.width(32)) comparator_2 (.a(register_1_q), .b(Data_In_0), .eq(comparator_2_eq));  // open: gt, lt
  Comparator #(.width(32)) comparator_3 (.a(register_2_q), .b(Data_In_1), .eq(comparator_3_eq));  // open: gt, lt
  Comparator #(.width(32)) comparator_4 (.a(register_3_q), .b(Data_In_2), .eq(comparator_4_eq));  // open: gt, lt
  Comparator #(.width(32)) comparator_5 (.a(register_4_q), .b(Data_In_3), .eq(comparator_5_eq));  // open: gt, lt
  Comparator #(.width(32)) comparator_6 (
    .a(register_5_q), .b({{11{1'b1}}, nRead_Write, Mask, Address}), .eq(comparator_6_eq));  // open: gt, lt
  nand nand_1 (nand_1_out, comparator_6_eq, comparator_2_eq, comparator_3_eq, comparator_4_eq, comparator_5_eq);
  and and_1 (Changed, nand_1_out, Chip_Select);
  or or_11 (Load, Count, Load1, Load0);
  and and_2 (and_2_out, Mask[0], Update_Mem, nRead_Write);
  and and_3 (and_3_out, Mask[1], Update_Mem, nRead_Write);
  and and_4 (and_4_out, Mask[2], Update_Mem, nRead_Write);
  and and_5 (and_5_out, Mask[3], Update_Mem, nRead_Write);
  RAM_part #(.addrWidth(16), .dataWidth(32), .bus("separate")) ram_1 (
    .addr(Address), .din(Data_In_0), .data(Data_Out_0), .str(and_2_out), .sel(Chip_Select), .clk(CLK),
    .ld(and_6_out), .clr(Reset));
  and and_6 (and_6_out, ~nRead_Write, Idle);  // AND_Gate
  RAM_part #(.addrWidth(16), .dataWidth(32), .bus("separate")) ram_2 (
    .addr(Address), .din(Data_In_1), .data(Data_Out_1), .str(and_3_out), .sel(Chip_Select), .clk(CLK),
    .ld(and_7_out), .clr(Reset));
  and and_7 (and_7_out, ~nRead_Write, Idle);  // AND_Gate
  RAM_part #(.addrWidth(16), .dataWidth(32), .bus("separate")) ram_3 (
    .addr(Address), .din(Data_In_2), .data(Data_Out_2), .str(and_4_out), .sel(Chip_Select), .clk(CLK),
    .ld(and_8_out), .clr(Reset));
  and and_8 (and_8_out, ~nRead_Write, Idle);  // AND_Gate
  RAM_part #(.addrWidth(16), .dataWidth(32), .bus("separate")) ram_4 (
    .addr(Address), .din(Data_In_3), .data(Data_Out_3), .str(and_5_out), .sel(Chip_Select), .clk(CLK),
    .ld(and_9_out), .clr(Reset));
  and and_9 (and_9_out, ~nRead_Write, Idle);  // AND_Gate

  assign Read_Time = 4'b0011;
  assign Write_Time = 4'b0010;

  // Other names for the same wires on the sheet: M0 = Mask[0]; M1 = Mask[1]; M2 = Mask[2]; M3 = Mask[3];
  //   RW = nRead_Write; CLR = Reset; CS = Chip_Select; Load2 = Count

  // Notes on the sheet:
  //   NO MODIFICAR
  //   excepto quizás los valores RT y WT
  //   BANK0
  //   BANK1
  //   BANK2
  //   BANK3
endmodule

module S_MIPS (
  input  Kbd_Available,
  input  [6:0] Kbd_ASCII_Data,
  input  [31:0] RAM_Out_0,
  input  [31:0] RAM_Out_1,
  input  Reset,
  input  [31:0] RAM_Out_2,
  input  Clock,
  input  [31:0] RAM_Out_3,
  input  [3:0] Read_Time,
  input  [3:0] Write_Time,
  output Kbd_Enable,
  output [15:0] Address,
  output Kbd_Clear,
  output TTY_Enable,
  output [6:0] TTY_ASCII_Data,
  output Stop,
  output [31:0] RAM_In_0,
  output [31:0] RAM_In_1,
  output [31:0] RAM_In_2,
  output [31:0] RAM_In_3,
  output [3:0] Mask,
  output nRead_Write,
  output Chip_Select
);


  // Other names for the same wires on the sheet: CLK = Clock; CLR = Reset; CS = Chip_Select;
  //   KBD_AVAIL = Kbd_Available; KBD_CLR = Kbd_Clear; KBD_DATA[6:0] = Kbd_ASCII_Data; RAM_A[15:0] = Address;
  //   RAM_INPUT_0[31:0] = RAM_In_0; RAM_INPUT_1[31:0] = RAM_In_1; RAM_INPUT_2[31:0] = RAM_In_2;
  //   RAM_INPUT_3[31:0] = RAM_In_3; RAM_MASK[3:0] = Mask; RAM_OUTPUT_0[31:0] = RAM_Out_0;
  //   RAM_OUTPUT_1[31:0] = RAM_Out_1; RAM_OUTPUT_2[31:0] = RAM_Out_2; RAM_OUTPUT_3[31:0] = RAM_Out_3;
  //   RW = nRead_Write; TTY_DATA[6:0] = TTY_ASCII_Data

  // Notes on the sheet:
  //   RAM ADDRESS
  //   DATA FROM RAM
  //   DATA TO RAM
  //   DATA WRITE MASK
  //   RAM TIMING
  //   RAM CONTROL
  //   KEYBOARD
  //   TTY
  //   SEQUENCING
endmodule

module RAM_Dispatcher (
  input  [3:0] WriteTime,
  input  Clock,
  input  CLR,
  output [31:0] Data,
  output [15:0] Address,
  output [3:0] Mask,
  output Finished,
  output Write
);

  wire demultiplexer_2_out1, demultiplexer_3_out1, End, IDLE_q, IncAddr, Load, or_1_out, or_2_out, While_q,
       WriteEnd;
  wire [3:0] counter_1_q;
  wire [31:0] CurrentAddress_q;

  Counter #(.width(32), .max('hffffffff)) CurrentAddress (
    .count(IncAddr), .Q({CurrentAddress_q[31:18], Address, CurrentAddress_q[1:0]}), .clk(Clock), .clr(CLR));  // open: load, D, carry
  or or_1 (or_1_out, IncAddr, demultiplexer_3_out1, Finished);
  D_Flip_Flop IDLE (.clk(Clock), .D(or_1_out), .Q(IDLE_q), .preset(CLR));  // open: Qn, en, reset
  Demultiplexer #(.enable("false")) demultiplexer_1 (.out0(Load), .out1(Finished), .in(IDLE_q), .sel(End));
  D_Flip_Flop While (.clk(Clock), .D(or_2_out), .Q(While_q), .reset(CLR));  // open: Qn, preset, en
  or or_2 (or_2_out, Write, Load);
  RAM_part #(.addrWidth(18), .dataWidth(32)) ram_1 (
    .addr({Address, CurrentAddress_q[1:0]}), .data(Data), .clk(Clock));  // open: sel, ld, clr
  Demultiplexer #(.enable("false")) demultiplexer_2 (
    .out0(Write), .out1(demultiplexer_2_out1), .in(While_q), .sel(WriteEnd));
  Decoder #(.select(2)) decoder_1 (
    .out0(Mask[0]), .out1(Mask[1]), .out2(Mask[2]), .out3(Mask[3]), .sel(CurrentAddress_q[1:0]));  // open: en
  Demultiplexer #(.enable("false")) demultiplexer_3 (
    .out0(IncAddr), .out1(demultiplexer_3_out1), .in(demultiplexer_2_out1), .sel(End));
  Counter #(.width(4), .max('hf)) counter_1 (
    .load(Load), .D(WriteTime), .count(Write), .Q(counter_1_q), .clk(Clock));  // open: carry, clr
  Comparator #(.width(32)) comparator_1 (.a(Data), .b({32{1'b1}}), .eq(End));  // open: gt, lt
  Comparator #(.width(4)) comparator_2 (.a(4'b0000), .b(counter_1_q), .eq(WriteEnd));  // open: gt, lt

  // Other names for the same wires on the sheet: CLK = Clock; Count = Write; WT[3:0] = WriteTime
endmodule

module Data_Path (
  input  [1:0] cs_RF_DI,
  input  cs_ALU_B_selector,
  input  cs_RF_SA_selector
);

  wire clk, ss_add, ss_addi, ss_and, ss_andi, ss_beq, ss_bgtz, ss_blez, ss_bltz, ss_bne, ss_div, ss_divu,
       ss_halt, ss_j, ss_jr, ss_kbd, ss_lw, ss_mfhi, ss_mflo, ss_mult, ss_mulu, ss_nop, ss_nor, ss_or,
       ss_ori, ss_pop, ss_push, ss_rnd, ss_slt, ss_slti, ss_sltiu, ss_sltu, ss_sub, ss_sw, ss_tty, ss_xor,
       ss_xori;
  wire [4:0] multiplexer_2_out, Rd, RF_DA, RF_ID_In, Rs, Rt;
  wire [5:0] func_code, op_code;
  wire [25:0] jump_dest;
  wire [31:0] A, ALU_result, B, constant, HI_value, ID_input, LO_value, multiplexer_3_out, RF_DI;

  Branch_Control_Unit branch_control_unit_1 ();  // open: IA, Jump, Constante, bne, bgtz, blez, bltz, j, jr, Rs, Rt, beq, Output
  ale_s_mips_Instruction_Decoder instruction_decoder_1 (
    .Input_from_the_RAM(ID_input), .nop(ss_nop), .add(ss_add), .sub(ss_sub), .mult(ss_mult), .mulu(ss_mulu),
    .div(ss_div), .divu(ss_divu), .slt(ss_slt), .sltu(ss_sltu), .\and (ss_and), .\or (ss_or), .\nor (ss_nor),
    .\xor (ss_xor), .addi(ss_addi), .slti(ss_slti), .sltiu(ss_sltiu), .andi(ss_andi), .ori(ss_ori),
    .xori(ss_xori), .lw(ss_lw), .sw(ss_sw), .pop(ss_pop), .push(ss_push), .beq(ss_beq), .bne(ss_bne),
    .blez(ss_blez), .bgtz(ss_bgtz), .bltz(ss_bltz), .j(ss_j), .jr(ss_jr), .mfhi(ss_mfhi), .mflo(ss_mflo),
    .halt(ss_halt), .tty(ss_tty), .rnd(ss_rnd), .kbd(ss_kbd), .func_code(func_code), .Rd(Rd), .Rt(Rt),
    .Rs(Rs), .op_code(op_code), .op_code_3(jump_dest));  // open: op_code_2
  Multiplexer #(.select(2), .width(32), .enable("false")) multiplexer_1 (
    .in0(ALU_result), .in1(HI_value), .in2(LO_value), .out(RF_DI), .sel(cs_RF_DI));  // open: in3
  Multiplexer #(.width(5), .enable("false")) multiplexer_2 (
    .in0(RF_ID_In), .in1({5{1'b1}}), .out(multiplexer_2_out), .sel(cs_RF_SA_selector));
  Register_File register_file_1 (
    .DA(RF_DA), .DI(RF_DI), .A(A), .B(B), .Clock(clk), .SA(multiplexer_2_out));  // open: RW, Rst, SB
  Multiplexer #(.width(32), .enable("false")) multiplexer_3 (
    .in0(B), .in1(constant), .out(multiplexer_3_out), .sel(cs_ALU_B_selector));
  ale_s_mips_ALU alu_1 (.A(multiplexer_3_out), .B(A), .Output(ALU_result));  // open: LO, HI, OP
endmodule

module Register_File (
  input  [4:0] DA,
  input  [31:0] DI,
  input  RW,
  input  Rst,
  input  Clock,
  input  [4:0] SA,
  input  [4:0] SB,
  output [31:0] A,
  output [31:0] B
);

  wire e0, e1, e2, e3, e4, e5, e6, e7, e8, e9, e10, e11, e12, e13, e14, e15, e16, e17, e18, e19, e20, e21,
       e22, e23, e24, e25, e26, e27, e28, e29, e30, e31;
  wire [31:0] S0, S1, S2, S3, S4, S5, S6, S7, S8, S9, S10, S11, S12, S13, S14, S15, S16, S17, S18, S19, S20,
       S21, S22, S23, S24, S25, S26, S27, S28, S29, S30, S31;

  Register #(.width(32)) R31 (.D(DI), .en(e31), .Q(S31), .clk(Clock), .clr(Rst));
  Register #(.width(32)) R23 (.D(DI), .en(e23), .Q(S23), .clk(Clock), .clr(Rst));
  Register #(.width(32)) R15 (.D(DI), .en(e15), .Q(S15), .clk(Clock), .clr(Rst));
  Register #(.width(32)) R7 (.D(DI), .en(e7), .Q(S7), .clk(Clock), .clr(Rst));
  Register #(.width(32)) R30 (.D(DI), .en(e30), .Q(S30), .clk(Clock), .clr(Rst));
  Register #(.width(32)) R22 (.D(DI), .en(e22), .Q(S22), .clk(Clock), .clr(Rst));
  Register #(.width(32)) R14 (.D(DI), .en(e14), .Q(S14), .clk(Clock), .clr(Rst));
  Register #(.width(32)) R6 (.D(DI), .en(e6), .Q(S6), .clk(Clock), .clr(Rst));
  Register #(.width(32)) R29 (.D(DI), .en(e29), .Q(S29), .clk(Clock), .clr(Rst));
  Register #(.width(32)) R21 (.D(DI), .en(e21), .Q(S21), .clk(Clock), .clr(Rst));
  Register #(.width(32)) R13 (.D(DI), .en(e13), .Q(S13), .clk(Clock), .clr(Rst));
  Register #(.width(32)) R5 (.D(DI), .en(e5), .Q(S5), .clk(Clock), .clr(Rst));
  Register #(.width(32)) R28 (.D(DI), .en(e28), .Q(S28), .clk(Clock), .clr(Rst));
  Register #(.width(32)) R20 (.D(DI), .en(e20), .Q(S20), .clk(Clock), .clr(Rst));
  Register #(.width(32)) R12 (.D(DI), .en(e12), .Q(S12), .clk(Clock), .clr(Rst));
  Register #(.width(32)) R4 (.D(DI), .en(e4), .Q(S4), .clk(Clock), .clr(Rst));
  Register #(.width(32)) R27 (.D(DI), .en(e27), .Q(S27), .clk(Clock), .clr(Rst));
  Register #(.width(32)) R19 (.D(DI), .en(e19), .Q(S19), .clk(Clock), .clr(Rst));
  Register #(.width(32)) R11 (.D(DI), .en(e11), .Q(S11), .clk(Clock), .clr(Rst));
  Register #(.width(32)) R3 (.D(DI), .en(e3), .Q(S3), .clk(Clock), .clr(Rst));
  Demultiplexer #(.select(5)) demultiplexer_1 (
    .out0(e0), .out1(e1), .out2(e2), .out3(e3), .out4(e4), .out5(e5), .out6(e6), .out7(e7), .out8(e8),
    .out9(e9), .out10(e10), .out11(e11), .out12(e12), .out13(e13), .out14(e14), .out15(e15), .out16(e16),
    .out17(e17), .out18(e18), .out19(e19), .out20(e20), .out21(e21), .out22(e22), .out23(e23), .out24(e24),
    .out25(e25), .out26(e26), .out27(e27), .out28(e28), .out29(e29), .out30(e30), .out31(e31), .in(RW),
    .sel(DA));  // open: en
  Register #(.width(32)) R26 (.D(DI), .en(e26), .Q(S26), .clk(Clock), .clr(Rst));
  Register #(.width(32)) R18 (.D(DI), .en(e18), .Q(S18), .clk(Clock), .clr(Rst));
  Register #(.width(32)) R10 (.D(DI), .en(e10), .Q(S10), .clk(Clock), .clr(Rst));
  Register #(.width(32)) R2 (.D(DI), .en(e2), .Q(S2), .clk(Clock), .clr(Rst));
  Register #(.width(32)) R25 (.D(DI), .en(e25), .Q(S25), .clk(Clock), .clr(Rst));
  Register #(.width(32)) R17 (.D(DI), .en(e17), .Q(S17), .clk(Clock), .clr(Rst));
  Register #(.width(32)) R9 (.D(DI), .en(e9), .Q(S9), .clk(Clock), .clr(Rst));
  Register #(.width(32)) R1 (.D(DI), .en(e1), .Q(S1), .clk(Clock), .clr(Rst));
  Register #(.width(32)) R24 (.D(DI), .en(e24), .Q(S24), .clk(Clock), .clr(Rst));
  Register #(.width(32)) R16 (.D(DI), .en(e16), .Q(S16), .clk(Clock), .clr(Rst));
  Register #(.width(32)) R8 (.D(DI), .en(e8), .Q(S8), .clk(Clock), .clr(Rst));
  Register #(.width(32)) R0 (.D({32{1'b0}}), .en(e0), .Q(S0), .clk(Clock), .clr(Rst));
  Multiplexer #(.select(5), .width(32)) multiplexer_1 (
    .in0(S0), .in1(S1), .in2(S2), .in3(S3), .in4(S4), .in5(S5), .in6(S6), .in7(S7), .in8(S8), .in9(S9),
    .in10(S10), .in11(S11), .in12(S12), .in13(S13), .in14(S14), .in15(S15), .in16(S16), .in17(S17),
    .in18(S18), .in19(S19), .in20(S20), .in21(S21), .in22(S22), .in23(S23), .in24(S24), .in25(S25),
    .in26(S26), .in27(S27), .in28(S28), .in29(S29), .in30(S30), .in31(S31), .out(A), .sel(SA));  // open: en
  Multiplexer #(.select(5), .width(32)) multiplexer_2 (
    .in0(S0), .in1(S1), .in2(S2), .in3(S3), .in4(S4), .in5(S5), .in6(S6), .in7(S7), .in8(S8), .in9(S9),
    .in10(S10), .in11(S11), .in12(S12), .in13(S13), .in14(S14), .in15(S15), .in16(S16), .in17(S17),
    .in18(S18), .in19(S19), .in20(S20), .in21(S21), .in22(S22), .in23(S23), .in24(S24), .in25(S25),
    .in26(S26), .in27(S27), .in28(S28), .in29(S29), .in30(S30), .in31(S31), .out(B), .sel(SB));  // open: en

  // Other names for the same wires on the sheet: c = Clock; D[31:0] = DI

  // Notes on the sheet:
  //   Registros
  //   Enables
  //   Salidas
  //   Selectores de salida
endmodule

module ALU (
  input  [31:0] A,
  input  [31:0] B,
  input  [5:0] OP,
  output [31:0] Output
);

  wire comparator_1_lt, comparator_2_lt;
  wire [31:0] \and , div_hi, div_lo, divu_hi, divu_lo, mul_hi, mul_lo, mulu_hi, mulu_lo, \nor , \or , slt,
       sltu, sub, sum, to_positive_1_output, to_positive_2_output, to_positive_3_output,
       to_positive_4_output, \xnor ;

  Adder #(.width(32)) adder_1 (.a(A), .b(B), .out(sum));  // open: cin, cout
  assign \and  = A & B;  // AND_Gate AND, 32 bits wide
  assign \or  = A | B;  // OR_Gate OR, 32 bits wide
  assign \nor  = ~(A | B);  // NOR_Gate NOR, 32 bits wide
  assign \xnor  = ~(A ^ B);  // XNOR_Gate XNOR, 32 bits wide
  Subtractor #(.width(32)) subtractor_1 (.a(A), .b(B), .out(sub));  // open: bin, bout
  Multiplier #(.width(32)) multiplier_1 (.a(A), .b(B), .out(mul_lo), .cout(mul_hi));  // open: cin
  to_positive to_positive_1 (.in_1(A), .Output(to_positive_1_output));
  to_positive to_positive_2 (.in_1(B), .Output(to_positive_2_output));
  Comparator #(.width(32)) comparator_1 (.a(A), .b(B), .lt(comparator_1_lt));  // open: gt, eq
  Multiplier #(.width(32)) multiplier_2 (
    .a(to_positive_1_output), .b(to_positive_2_output), .out(mulu_lo), .cout(mulu_hi));  // open: cin
  Multiplexer #(.width(32)) multiplexer_1 (
    .in0({32{1'b0}}), .in1(32'h1), .out(slt), .sel(comparator_1_lt));  // open: en
  Divider #(.width(32)) divider_1 (.a(A), .b(B), .out(div_lo), .rem(div_hi));  // open: upper
  to_positive to_positive_3 (.in_1(A), .Output(to_positive_3_output));
  to_positive to_positive_4 (.in_1(B), .Output(to_positive_4_output));
  Comparator #(.width(32), .mode("unsigned")) comparator_2 (.a(A), .b(B), .lt(comparator_2_lt));  // open: gt, eq
  Divider #(.width(32)) divider_2 (
    .a(to_positive_3_output), .b(to_positive_4_output), .out(divu_lo), .rem(divu_hi));  // open: upper
  Multiplexer #(.width(32)) multiplexer_2 (
    .in0({32{1'b0}}), .in1(32'h1), .out(sltu), .sel(comparator_2_lt));  // open: en
  RAM ram_1 ();  // open: Address, Data_Out_0, Data_Out_1, Data_Out_2, Data_Out_3, Data_In_0, Data_In_1, Data_In_2, Data_In_3, Mask, nRead_Write, Chip_Select, Read_Time, Reset, Write_Time

  // Notes on the sheet:
  //   Suma
  //   Lógicos
  //   Resta
  //   Set last then
  //   Multiplicación
  //   Multiplicación U
  //   División
  //   División U
  //   Set last then U
endmodule

module Branch_Control_Unit (
  input  [31:0] IA,
  input  [15:0] Constante,
  input  [25:0] Jump,
  input  [31:0] Rs,
  input  [31:0] Rt,
  input  beq,
  input  bne,
  input  bgtz,
  input  blez,
  input  bltz,
  input  j,
  input  jr,
  output [31:0] Output
);

  wire and_1_out, and_2_out, and_3_out, and_4_out, and_5_out, beq_t, bgtz_t, blez_t, bltz_t, bne_t,
       comparator_2_eq, or_3_out;
  wire [0:0] or_2_out;
  wire [15:0] Const_4;
  wire [31:0] IA_4, jmp_cond_result, multiplexer_1_out;

  Comparator #(.width(32)) comparator_1 (.a(Rs), .b(Rt), .gt(bne_t), .eq(beq_t), .lt(bne_t));
  Comparator #(.width(32)) comparator_2 (.a(Rs), .b({32{1'b0}}), .gt(bgtz_t), .eq(comparator_2_eq), .lt(bltz_t));
  and and_1 (and_1_out, beq, beq_t);
  and and_2 (and_2_out, bne, bne_t);
  and and_3 (and_3_out, bgtz, bgtz_t);
  and and_4 (and_4_out, blez, blez_t);
  and and_5 (and_5_out, bltz, bltz_t);
  or or_1 (blez_t, comparator_2_eq, bltz_t);
  or or_2 (or_2_out[0], and_1_out, and_2_out, and_3_out, and_4_out, and_5_out);
  Multiplexer #(.select(2), .width(32), .enable("false")) multiplexer_1 (
    .in0(Rs), .in1(jmp_cond_result), .in2({IA[31:28], Jump, 2'b00}), .out(multiplexer_1_out),
    .sel({j, or_2_out[0]}));  // open: in3
  or or_3 (or_3_out, j, or_2_out[0], jr);
  Multiplexer #(.width(32), .enable("false")) multiplexer_2 (
    .in0(IA_4), .in1(multiplexer_1_out), .out(Output), .sel(or_3_out));
  Shifter #(.width(16)) shifter_1 (.in(Constante), .\dist (4'b0010), .out(Const_4));
  Adder #(.width(32)) adder_1 (.a(IA), .b(32'h4), .out(IA_4));  // open: cin, cout
  Adder #(.width(32)) adder_2 (.a({{16{1'b0}}, Const_4}), .b(IA_4), .out(jmp_cond_result));  // open: cin, cout

  // Other names for the same wires on the sheet: beq_f = beq; bgtz_f = bgtz; blez_f = blez; bltz_f = bltz;
  //   bne_f = bne; Const[15:0] = Constante; IA_conc_J[31:2] = {IA[31:28], Jump}

  // Notes on the sheet:
  //   Inputs
  //   Comparators
  //   Defining Conditional Jump
  //   Defining Jump
endmodule

module to_positive (
  input  [31:0] in_1,
  output [31:0] Output
);

  wire n;
  wire [31:0] minus_in;

  Negator #(.width(32)) negator_1 (.in(in_1), .out(minus_in));
  Comparator #(.width(32)) comparator_1 (.a(in_1), .b({32{1'b0}}), .lt(n));  // open: gt, eq
  Multiplexer #(.width(32)) multiplexer_1 (.in0(in_1), .in1(minus_in), .out(Output), .sel(n));  // open: en

  // Other names for the same wires on the sheet: in[31:0] = in_1
endmodule

module Control_Unit (
  input  [3:0] Read_Time,
  input  [3:0] Write_Time,
  input  Clock,
  input  start,
  input  reset,
  input  nop,
  input  addi,
  input  add,
  input  slti,
  input  sub,
  input  sltiu,
  input  mult,
  input  andi,
  input  mulu,
  input  ori,
  input  div,
  input  xori,
  input  divu,
  input  lw,
  input  slt,
  input  sw,
  input  sltu,
  input  beq,
  input  \and ,
  input  bne,
  input  \or ,
  input  blez,
  input  \nor ,
  input  bgtz,
  input  \xor ,
  input  bltz,
  input  pop,
  input  push,
  input  jr,
  input  j,
  input  mfhi,
  input  mflo,
  input  halt,
  input  tty,
  input  rnd,
  input  kbd
);

  wire clock_t, demultiplexer_1_out0, demultiplexer_1_out1, IDDLE_q, Ready;

  D_Flip_Flop #(.trigger("falling")) IDDLE (
    .clk(clock_t), .D(demultiplexer_1_out0), .Q(IDDLE_q), .en(start), .reset(reset));  // open: Qn, preset
  Demultiplexer #(.enable("false")) demultiplexer_1 (
    .out0(demultiplexer_1_out0), .out1(demultiplexer_1_out1), .in(IDDLE_q), .sel(Ready));
  Demultiplexer #(.enable("false")) demultiplexer_2 (.in(demultiplexer_1_out1));  // open: out0, out1, sel

  // Other names for the same wires on the sheet: RT[3:0] = Read_Time; WT[3:0] = Write_Time

  // Notes on the sheet:
  //   R Type
  //   I Type
  //   J Type
endmodule

module slw_direction (
  input  [31:0] Rs,
  input  [15:0] offset_id,
  output [31:0] Direction_Output
);

  wire [31:0] I, Rest;

  Adder #(.width(32)) adder_1 (.a(Rs), .b({{17{offset_id[15]}}, offset_id[14:0]}), .out(I));  // open: cin, cout
  Divider #(.width(32)) divider_1 (.a(I), .b(32'h4), .rem(Rest));  // open: out, upper
  Subtractor #(.width(32)) subtractor_1 (.a(I), .b(Rest), .out(Direction_Output));  // open: bin, bout
endmodule

module test (
  input  [15:0] j,
  input  [15:0] j_2,
  output [15:0] Output,
  output [15:0] Output_2
);

  Multiplier #(.width(16)) multiplier_1 (.a(j), .b(j_2), .out(Output_2));  // open: cin, cout
  Shifter #(.width(16)) shifter_1 (.in(j), .\dist (4'b0010), .out(Output));
  // Probe on 4'b0010
endmodule
