// Logisim project s-mips.circ as structural Verilog: 18 circuits, main circuit S-MIPS Board
module S_MIPS_Board (
  input  DESHABILITAR_DISPATCHER,
  output halt
);

  wire button_1_out, CLK, CS, d_ff_1_q, LCLR, LoadRAM, LoadRAMOn, LW, R_R_W, R_W, ram_dispatcher_1_finished,
       RCS, Reset_out, RST, TTY_EN;
  wire [2:0] KDB;
  wire [3:0] LMask, Mask, ram_1_read_time, ram_1_write_time, RMask;
  wire [6:0] KDB_DATA, TTY_DATA;
  wire [15:0] Addr, LAddr, RAddr;
  wire [31:0] I0, I1, I2, I3, LData, ram_1_data_out_0, ram_1_data_out_1, ram_1_data_out_2, ram_1_data_out_3,
       RI0, RI1, RI2, RI3;

  TTY #(.rows(25), .cols(80)) tty_1 (.data(TTY_DATA), .clk(CLK), .we(TTY_EN), .clr(RST));
  not not_1 (LoadRAMOn, ram_dispatcher_1_finished);
  RAM_Dispatcher ram_dispatcher_1 (
    .WriteTime(ram_1_write_time), .Clock(CLK), .Data(LData), .Address(LAddr), .Mask(LMask),
    .Finished(ram_dispatcher_1_finished), .Write(LW), .CLR(LCLR));
  Keyboard #(.buflen(64)) keyboard_1 (.clk(CLK), .re(KDB[0]), .avail(KDB[2]), .data(KDB_DATA));  // open: clr
  RAM ram_1 (
    .Address(RAddr), .Data_Out_0(ram_1_data_out_0), .Data_Out_1(ram_1_data_out_1),
    .Data_Out_2(ram_1_data_out_2), .Data_Out_3(ram_1_data_out_3), .Data_In_0(RI0), .Data_In_1(RI1),
    .Data_In_2(RI2), .Data_In_3(RI3), .Mask(RMask), .nRead_Write(R_R_W), .Chip_Select(RCS),
    .Read_Time(ram_1_read_time), .Reset(button_1_out), .Write_Time(ram_1_write_time));
  Button button_1 (.out(button_1_out));
  D_Flip_Flop d_ff_1 (.clk(CLK), .D(1'b1), .Q(d_ff_1_q), .reset(Reset_out));  // open: Qn, preset, en
  Button Reset (.out(Reset_out));
  S_MIPS s_mips_1 (
    .Kbd_Enable(KDB[0]), .Address(Addr), .Kbd_Clear(KDB[1]), .Kbd_Available(KDB[2]), .RAM_In_0(I0),
    .Kbd_ASCII_Data(KDB_DATA), .RAM_In_1(I1), .TTY_Enable(TTY_EN), .RAM_In_2(I2), .RAM_In_3(I3),
    .TTY_ASCII_Data(TTY_DATA), .Reset(RST), .RAM_Out_0(ram_1_data_out_0), .Clock(CLK),
    .RAM_Out_1(ram_1_data_out_1), .Stop(halt), .RAM_Out_2(ram_1_data_out_2), .RAM_Out_3(ram_1_data_out_3),
    .Mask(Mask), .Read_Time(ram_1_read_time), .Write_Time(ram_1_write_time), .nRead_Write(R_W),
    .Chip_Select(CS));
  D_Flip_Flop d_ff_2 (.clk(CLK), .D(d_ff_1_q), .Qn(LCLR), .reset(Reset_out));  // open: Q, preset, en
  or or_1 (RST, LCLR, LoadRAM);
  Clock clock_1 (.out(CLK));
  Multiplexer #(.width(32), .enable("false")) multiplexer_1 (.in0(I0), .in1(LData), .out(RI0), .sel(LoadRAM));
  Multiplexer #(.width(32), .enable("false")) multiplexer_2 (.in0(I1), .in1(LData), .out(RI1), .sel(LoadRAM));
  Multiplexer #(.width(32), .enable("false")) multiplexer_3 (.in0(I2), .in1(LData), .out(RI2), .sel(LoadRAM));
  Multiplexer #(.width(32), .enable("false")) multiplexer_4 (.in0(I3), .in1(LData), .out(RI3), .sel(LoadRAM));
  and and_1 (LoadRAM, ~DESHABILITAR_DISPATCHER, LoadRAMOn);  // AND_Gate
  Multiplexer #(.width(16), .enable("false")) multiplexer_5 (.in0(Addr), .in1(LAddr), .out(RAddr), .sel(LoadRAM));
  Multiplexer #(.width(4), .enable("false")) multiplexer_6 (.in0(Mask), .in1(LMask), .out(RMask), .sel(LoadRAM));
  Multiplexer #(.enable("false")) multiplexer_7 (.in0(CS), .in1(LW), .out(RCS), .sel(LoadRAM));
  Multiplexer #(.enable("false")) multiplexer_8 (.in0(R_W), .in1(LW), .out(R_R_W), .sel(LoadRAM));

  // Notes on the sheet:
  //   NO MODIFICAR
  //   Keyboard
endmodule

module RAM (
  input  [15:0] Address,
  input  [31:0] Data_In_0,
  input  [31:0] Data_In_1,
  input  [31:0] Data_In_2,
  input  [31:0] Data_In_3,
  input  [3:0] Mask,
  input  nRead_Write,
  input  Chip_Select,
  input  Reset,
  output [31:0] Data_Out_0,
  output [31:0] Data_Out_1,
  output [31:0] Data_Out_2,
  output [31:0] Data_Out_3,
  output [3:0] Read_Time,
  output [3:0] Write_Time
);

  wire and_2_out, and_3_out, and_4_out, and_5_out, and_6_out, and_7_out, and_8_out, and_9_out, Changed, CLK,
       comparator_2_eq, comparator_3_eq, comparator_4_eq, comparator_5_eq, comparator_6_eq, Count,
       demultiplexer_3_out0, Idle, Idle_q, Load, Load0, Load1, nand_1_out, or_1_out, or_2_out, or_3_out,
       or_4_out, or_5_out, or_6_out, or_7_out, or_8_out, or_9_out, or_10_out, Proc_q, Update_Mem, Zero_Time;
  wire [3:0] counter_1_q, multiplexer_1_out, subtractor_1_out;
  wire [31:0] register_1_q, register_2_q, register_3_q, register_4_q, register_5_q;

  // Probe on 4'b0011
  // Probe on 4'b0010
  Multiplexer #(.width(4), .enable("false")) multiplexer_1 (
    .in0(4'b0011), .in1(4'b0010), .out(multiplexer_1_out), .sel(nRead_Write));
  or or_1 (or_1_out, Idle, Update_Mem);
  or or_2 (or_2_out, ~Chip_Select, Reset);  // OR_Gate
  Subtractor #(.width(4)) subtractor_1 (.a(multiplexer_1_out), .b(4'b0010), .out(subtractor_1_out));  // open: bin, bout
  Demultiplexer #(.enable("false")) demultiplexer_1 (.out0(Idle), .out1(Load0), .in(Idle_q), .sel(Changed));
  D_Flip_Flop u_Idle (.clk(CLK), .D(or_1_out), .Q(Idle_q), .preset(or_2_out));  // open: Qn, en, reset
  // Probe on counter_1_q
  Counter #(.width(4), .max('hf)) counter_1 (
    .load(Load), .D(subtractor_1_out), .count(Count), .Q(counter_1_q), .clk(CLK), .clr(or_3_out));  // open: carry
  or or_3 (or_3_out, ~Chip_Select, Reset);  // OR_Gate
  Comparator #(.width(4), .mode("unsigned")) comparator_1 (
    .a(4'b0000), .b(counter_1_q), .eq(Zero_Time));  // open: gt, lt
  or or_4 (or_4_out, Count, Load0, Load1);
  Register #(.width(32)) register_1 (.D(Data_In_0), .en(Chip_Select), .Q(register_1_q), .clk(CLK), .clr(or_5_out));
  or or_5 (or_5_out, ~Chip_Select, Reset);  // OR_Gate
  Register #(.width(32)) register_2 (.D(Data_In_1), .en(Chip_Select), .Q(register_2_q), .clk(CLK), .clr(or_6_out));
  or or_6 (or_6_out, ~Chip_Select, Reset);  // OR_Gate
  Register #(.width(32)) register_3 (.D(Data_In_2), .en(Chip_Select), .Q(register_3_q), .clk(CLK), .clr(or_7_out));
  or or_7 (or_7_out, ~Chip_Select, Reset);  // OR_Gate
  Register #(.width(32)) register_4 (.D(Data_In_3), .en(Chip_Select), .Q(register_4_q), .clk(CLK), .clr(or_8_out));
  or or_8 (or_8_out, ~Chip_Select, Reset);  // OR_Gate
  Register #(.width(32)) register_5 (
    .D({{11{1'b1}}, nRead_Write, Mask, Address}), .en(Chip_Select), .Q(register_5_q), .clk(CLK),
    .clr(or_9_out));
  or or_9 (or_9_out, ~Chip_Select, Reset);  // OR_Gate
  D_Flip_Flop Proc (.clk(CLK), .D(or_4_out), .Q(Proc_q), .reset(or_10_out));  // open: Qn, preset, en
  or or_10 (or_10_out, ~Chip_Select, Reset);  // OR_Gate
  Demultiplexer #(.enable("false")) demultiplexer_2 (
    .out0(Count), .out1(Update_Mem), .in(demultiplexer_3_out0), .sel(Zero_Time));
  Demultiplexer #(.enable("false")) demultiplexer_3 (
    .out0(demultiplexer_3_out0), .out1(Load1), .in(Proc_q), .sel(Changed));
  Clock clock_1 (.out(CLK));
  Comparator #(.width(32)) comparator_2 (.a(register_1_q), .b(Data_In_0), .eq(comparator_2_eq));  // open: gt, lt
  Comparator #(.width(32)) comparator_3 (.a(register_2_q), .b(Data_In_1), .eq(comparator_3_eq));  // open: gt, lt
  Comparator #(.width(32)) comparator_4 (.a(register_3_q), .b(Data_In_2), .eq(comparator_4_eq));  // open: gt, lt
  Comparator #(.width(32)) comparator_5 (.a(register_4_q), .b(Data_In_3), .eq(comparator_5_eq));  // open: gt, lt
  Comparator #(.width(32)) comparator_6 (
    .a(register_5_q), .b({{11{1'b1}}, nRead_Write, Mask, Address}), .eq(comparator_6_eq));  // open: gt, lt
  nand nand_1 (nand_1_out, comparator_6_eq, comparator_2_eq, comparator_3_eq, comparator_4_eq, comparator_5_eq);
  and and_1 (Changed, nand_1_out, Chip_Select);
  or or_11 (Load, Count, Load1, Load0);
  and and_2 (and_2_out, Mask[0], Update_Mem, nRead_Write);
  and and_3 (and_3_out, Mask[1], Update_Mem, nRead_Write);
  and and_4 (and_4_out, Mask[2], Update_Mem, nRead_Write);
  and and_5 (and_5_out, Mask[3], Update_Mem, nRead_Write);
  RAM_part #(.addrWidth(16), .dataWidth(32), .bus("separate")) ram_1 (
    .addr(Address), .din(Data_In_0), .data(Data_Out_0), .str(and_2_out), .sel(Chip_Select), .clk(CLK),
    .ld(and_6_out), .clr(Reset));
  and and_6 (and_6_out, ~nRead_Write, Idle);  // AND_Gate
  RAM_part #(.addrWidth(16), .dataWidth(32), .bus("separate")) ram_2 (
    .addr(Address), .din(Data_In_1), .data(Data_Out_1), .str(and_3_out), .sel(Chip_Select), .clk(CLK),
    .ld(and_7_out), .clr(Reset));
  and and_7 (and_7_out, ~nRead_Write, Idle);  // AND_Gate
  RAM_part #(.addrWidth(16), .dataWidth(32), .bus("separate")) ram_3 (
    .addr(Address), .din(Data_In_2), .data(Data_Out_2), .str(and_4_out), .sel(Chip_Select), .clk(CLK),
    .ld(and_8_out), .clr(Reset));
  and and_8 (and_8_out, ~nRead_Write, Idle);  // AND_Gate
  RAM_part #(.addrWidth(16), .dataWidth(32), .bus("separate")) ram_4 (
    .addr(Address), .din(Data_In_3), .data(Data_Out_3), .str(and_5_out), .sel(Chip_Select), .clk(CLK),
    .ld(and_9_out), .clr(Reset));
  and and_9 (and_9_out, ~nRead_Write, Idle);  // AND_Gate

  assign Read_Time = 4'b0011;
  assign Write_Time = 4'b0010;

  // Other names for the same wires on the sheet: M0 = Mask[0]; M1 = Mask[1]; M2 = Mask[2]; M3 = Mask[3];
  //   RW = nRead_Write; CLR = Reset; CS = Chip_Select; Load2 = Count

  // Notes on the sheet:
  //   NO MODIFICAR
  //   excepto quizás los valores RT y WT
  //   BANK0
  //   BANK1
  //   BANK2
  //   BANK3
endmodule

module S_MIPS (
  input  Kbd_Available,
  input  [6:0] Kbd_ASCII_Data,
  input  [31:0] RAM_Out_0,
  input  [31:0] RAM_Out_1,
  input  Reset,
  input  [31:0] RAM_Out_2,
  input  Clock,
  input  [31:0] RAM_Out_3,
  input  [3:0] Read_Time,
  input  [3:0] Write_Time,
  output Kbd_Enable,
  output [15:0] Address,
  output Kbd_Clear,
  output TTY_Enable,
  output [6:0] TTY_ASCII_Data,
  output Stop,
  output [31:0] RAM_In_0,
  output [31:0] RAM_In_1,
  output [31:0] RAM_In_2,
  output [31:0] RAM_In_3,
  output [3:0] Mask,
  output nRead_Write,
  output Chip_Select
);

  wire add_f, addi_f, and_f, andi_f, beq_f, bgtz_f, blez_f, bltz_f, bne_f, cs_KBD, cs_LO_HI,
       cs_Load_Instruction, cs_LOAD_TTY, cs_M, cs_M_PC_value, cs_NEW_RANDOM, cs_R_W, cs_R_W_PC, cs_RESET,
       cs_RF_DA, cs_RF_DA_SP, cs_RF_SB, div_f, divu_f, halt_f, j_f, jr_f, kbd_f, lw_f, mfhi_f, mflo_f,
       mult_f, mulu_f, nop_f, nor_f, or_f, ori_f, pop_f, push_f, RAM_r_w_DONE, rnd_f, slt_f, slti_f, sltiu_f,
       sltu_f, Start_Wait, sub_f, sw_f, tty_f, xor_f, xori_f;
  wire [1:0] cs_ALU_SELECT_B, cs_RF_DI, cs_RF_SA, Offset;
  wire [3:0] cs_ALU_OP;
  wire [31:0] RAM_Read, To_RAM;

  Waiter waiter_1 (
    .in_1(Start_Wait), .in_2(nRead_Write), .in_3(Read_Time), .in_4(Write_Time), .in_5(Clock),
    .Wait_Finish(RAM_r_w_DONE));
  Control_Unit control_unit_1 (
    .add(add_f), .slt(slt_f), .\and (and_f), .\nor (nor_f), .mult(mult_f), .div(div_f), .sub(sub_f),
    .sltu(sltu_f), .\or (or_f), .\xor (xor_f), .mulu(mulu_f), .divu(divu_f), .addi(addi_f), .slti(slti_f),
    .ori(ori_f), .j(j_f), .bgtz(bgtz_f), .beq(beq_f), .blez(blez_f), .andi(andi_f), .sltiu(sltiu_f),
    .xori(xori_f), .jr(jr_f), .bltz(bltz_f), .bne(bne_f), .nop(nop_f), .halt(halt_f), .rnd(rnd_f), .lw(lw_f),
    .pop(pop_f), .tty(tty_f), .kbd(kbd_f), .sw(sw_f), .push(push_f), .mfhi(mfhi_f), .Clk(Clock),
    .mflo(mflo_f), .R_W_done(RAM_r_w_DONE), .Circ_Reset(Reset), .Halt_2(Stop), .TTY_Enable(TTY_Enable),
    .CS_ALU_OP(cs_ALU_OP), .CS_RF_DA_SP(cs_RF_DA_SP), .CS_R_W(cs_R_W), .CS_RF_DI(cs_RF_DI),
    .CS_ALU_SELECT_B(cs_ALU_SELECT_B), .CS_RF_SA(cs_RF_SA), .CS_RF_DA(cs_RF_DA), .CS_RF_SB(cs_RF_SB),
    .CS_M(cs_M), .Read_or_Write_PC(cs_R_W_PC), .CS_M_PC_value(cs_M_PC_value), .Reset(cs_RESET),
    .CS_LO_HI(cs_LO_HI), .CS_NEW_RANDOM(cs_NEW_RANDOM), .CS_KBD(cs_KBD), .CS_LOAD_TTY(cs_LOAD_TTY),
    .RAM_R_W(nRead_Write), .KBD_Enable(Kbd_Enable), .KBD_Avaliable(Kbd_Available),
    .cs_Load_Instruction(cs_Load_Instruction), .Start_R_W(Start_Wait), .Chip_Select(Chip_Select));
  RAM_Writer ram_writer_1 (
    .offset(Offset), .Input(To_RAM), .Output(RAM_In_0), .Output_2(RAM_In_1), .Output_3(RAM_In_2),
    .Output_4(RAM_In_3), .Mask(Mask));
  RAM_Reader ram_reader_1 (
    .RAM_Input_1(RAM_Out_0), .RAM_Input_2(RAM_Out_1), .RAM_Input_3(RAM_Out_2), .RAM_Input_4(RAM_Out_3),
    .offset(Offset), .RAM_Input_Selected(RAM_Read));
  Data_Path data_path_1 (
    .CS_ALU_OP(cs_ALU_OP), .CS_ALU_SELECT_B(cs_ALU_SELECT_B), .CS_RF_DA(cs_RF_DA), .CS_RF_DA_SP(cs_RF_DA_SP),
    .CS_RF_DI(cs_RF_DI), .CS_RF_SA(cs_RF_SA), .CS_RF_SB(cs_RF_SB), .CS_M(cs_M),
    .CS_M_PC_value(cs_M_PC_value), .CS_LO_HI(cs_LO_HI), .Read_or_Write(cs_R_W), .Read_or_Write_PC(cs_R_W_PC),
    .Reset(cs_RESET), .CS_NEW_RANDOM(cs_NEW_RANDOM), .CS_KBD(cs_KBD), .CS_LOAD_TTY(cs_LOAD_TTY),
    .cs_kbd_aviable(Kbd_Available), .TTY_ASCII_Data(TTY_ASCII_Data), .Clock(Clock), .Offset(Offset),
    .Kbd_ASCII_Data(Kbd_ASCII_Data), .RAM_Direction(Address), .To_RAM(To_RAM), .RAM_Lecture(RAM_Read),
    .add(add_f), .slt(slt_f), .\and (and_f), .\nor (nor_f), .mult(mult_f), .div(div_f), .sub(sub_f),
    .sltu(sltu_f), .\or (or_f), .\xor (xor_f), .mulu(mulu_f), .divu(divu_f), .addi(addi_f), .slti(slti_f),
    .ori(ori_f), .j(j_f), .bgtz(bgtz_f), .beq(beq_f), .blez(blez_f), .andi(andi_f), .sltiu(sltiu_f),
    .xori(xori_f), .jr(jr_f), .bltz(bltz_f), .bne(bne_f), .nop(nop_f), .halt(halt_f), .rnd(rnd_f), .lw(lw_f),
    .pop(pop_f), .tty(tty_f), .kbd(kbd_f), .sw(sw_f), .push(push_f), .mfhi(mfhi_f), .mflo(mflo_f),
    .cs_Load_Instruction(cs_Load_Instruction));  // open: Input_From_RAM

  // Other names for the same wires on the sheet: CLK = Clock; CLR = Reset; CS = Chip_Select;
  //   KBD_AVAIL = Kbd_Available; KBD_CLR = Kbd_Clear; KBD_DATA[6:0] = Kbd_ASCII_Data; RAM_A[15:0] = Address;
  //   RAM_INPUT_0[31:0] = RAM_In_0; RAM_INPUT_1[31:0] = RAM_In_1; RAM_INPUT_2[31:0] = RAM_In_2;
  //   RAM_INPUT_3[31:0] = RAM_In_3; RAM_MASK[3:0] = Mask; RAM_OUTPUT_0[31:0] = RAM_Out_0;
  //   RAM_OUTPUT_1[31:0] = RAM_Out_1; RAM_OUTPUT_2[31:0] = RAM_Out_2; RAM_OUTPUT_3[31:0] = RAM_Out_3;
  //   RW = nRead_Write; TTY_DATA[6:0] = TTY_ASCII_Data

  // Notes on the sheet:
  //   RAM ADDRESS
  //   DATA FROM RAM
  //   DATA TO RAM
  //   DATA WRITE MASK
  //   RAM TIMING
  //   RAM CONTROL
  //   KEYBOARD
  //   TTY
  //   SEQUENCING
endmodule

module RAM_Dispatcher (
  input  [3:0] WriteTime,
  input  Clock,
  input  CLR,
  output [31:0] Data,
  output [15:0] Address,
  output [3:0] Mask,
  output Finished,
  output Write
);

  wire demultiplexer_2_out1, demultiplexer_3_out1, End, IDLE_q, IncAddr, Load, or_1_out, or_2_out, While_q,
       WriteEnd;
  wire [3:0] counter_1_q;
  wire [31:0] CurrentAddress_q;

  Counter #(.width(32), .max('hffffffff)) CurrentAddress (
    .count(IncAddr), .Q({CurrentAddress_q[31:18], Address, CurrentAddress_q[1:0]}), .clk(Clock), .clr(CLR));  // open: load, D, carry
  or or_1 (or_1_out, IncAddr, demultiplexer_3_out1, Finished);
  D_Flip_Flop IDLE (.clk(Clock), .D(or_1_out), .Q(IDLE_q), .preset(CLR));  // open: Qn, en, reset
  Demultiplexer #(.enable("false")) demultiplexer_1 (.out0(Load), .out1(Finished), .in(IDLE_q), .sel(End));
  D_Flip_Flop While (.clk(Clock), .D(or_2_out), .Q(While_q), .reset(CLR));  // open: Qn, preset, en
  or or_2 (or_2_out, Write, Load);
  RAM_part #(.addrWidth(18), .dataWidth(32)) ram_1 (
    .addr({Address, CurrentAddress_q[1:0]}), .data(Data), .clk(Clock));  // open: sel, ld, clr
  Demultiplexer #(.enable("false")) demultiplexer_2 (
    .out0(Write), .out1(demultiplexer_2_out1), .in(While_q), .sel(WriteEnd));
  Decoder #(.select(2)) decoder_1 (
    .out0(Mask[0]), .out1(Mask[1]), .out2(Mask[2]), .out3(Mask[3]), .sel(CurrentAddress_q[1:0]));  // open: en
  Demultiplexer #(.enable("false")) demultiplexer_3 (
    .out0(IncAddr), .out1(demultiplexer_3_out1), .in(demultiplexer_2_out1), .sel(End));
  Counter #(.width(4), .max('hf)) counter_1 (
    .load(Load), .D(WriteTime), .count(Write), .Q(counter_1_q), .clk(Clock));  // open: carry, clr
  Comparator #(.width(32)) comparator_1 (.a(Data), .b({32{1'b1}}), .eq(End));  // open: gt, lt
  Comparator #(.width(4)) comparator_2 (.a(4'b0000), .b(counter_1_q), .eq(WriteEnd));  // open: gt, lt

  // Other names for the same wires on the sheet: CLK = Clock; Count = Write; WT[3:0] = WriteTime
endmodule

module Data_Path (
  input  [3:0] CS_ALU_OP,
  input  [1:0] CS_ALU_SELECT_B,
  input  CS_RF_DA,
  input  CS_RF_DA_SP,
  input  [1:0] CS_RF_DI,
  input  [1:0] CS_RF_SA,
  input  CS_RF_SB,
  input  CS_M,
  input  CS_M_PC_value,
  input  CS_LO_HI,
  input  Read_or_Write,
  input  Read_or_Write_PC,
  input  Reset,
  input  CS_NEW_RANDOM,
  input  CS_KBD,
  input  CS_LOAD_TTY,
  input  cs_kbd_aviable,
  input  cs_Load_Instruction,
  input  Clock,
  input  [6:0] Kbd_ASCII_Data,
  input  [31:0] Input_From_RAM,
  input  [31:0] RAM_Lecture,
  output add,
  output slt,
  output \and ,
  output \nor ,
  output mult,
  output div,
  output sub,
  output sltu,
  output \or ,
  output \xor ,
  output mulu,
  output divu,
  output [6:0] TTY_ASCII_Data,
  output addi,
  output slti,
  output ori,
  output j,
  output bgtz,
  output beq,
  output blez,
  output [1:0] Offset,
  output andi,
  output sltiu,
  output xori,
  output jr,
  output bltz,
  output bne,
  output nop,
  output [15:0] RAM_Direction,
  output halt,
  output rnd,
  output lw,
  output pop,
  output [31:0] To_RAM,
  output tty,
  output kbd,
  output sw,
  output push,
  output mfhi,
  output mflo
);

  wire [4:0] multiplexer_2_out, multiplexer_5_out, multiplexer_9_out, multiplexer_10_out, Rd, Rs, Rt;
  wire [5:0] func_code, op_code;
  wire [15:0] b_constant;
  wire [25:0] jump_dest;
  wire [31:0] A, Alu_Hi, Alu_Lo, BC_Output, Constant, divider_1_rem, F, Hi, KBD_DATA, Lo, multiplexer_3_out,
       multiplexer_4_out, multiplexer_6_out, multiplexer_7_out, multiplexer_8_out, multiplexer_11_out,
       PC_value, random_val, register_1_q, subtractor_1_out;

  Multiplexer #(.width(32), .enable("false")) multiplexer_1 (
    .in0({32{1'b1}}), .in1({{25{1'b0}}, Kbd_ASCII_Data}), .out(KBD_DATA), .sel(cs_kbd_aviable));
  Register #(.width(32), .trigger("falling")) PC (
    .D(BC_Output), .en(Read_or_Write_PC), .Q(PC_value), .clk(Clock), .clr(Reset));
  // Probe on RAM_Lecture
  Branch_Control_Unit branch_control_unit_1 (
    .IA(PC_value), .Constante(b_constant), .Jump(jump_dest), .Rs(A), .Rt(To_RAM), .beq(beq), .bne(bne),
    .bgtz(bgtz), .blez(blez), .bltz(bltz), .j(j), .jr(jr), .Output(BC_Output));
  Register #(.width(32), .trigger("falling")) register_1 (
    .D(RAM_Lecture), .en(cs_Load_Instruction), .Q(register_1_q), .clk(Clock), .clr(Reset));
  // Probe on register_1_q
  Instruction_Decoder instruction_decoder_1 (
    .Input_from_the_RAM(register_1_q), .nop(nop), .add(add), .div(div), .\and (\and ), .j(j), .jr(jr),
    .sub(sub), .divu(divu), .\or (\or ), .mult(mult), .slt(slt), .\nor (\nor ), .mulu(mulu), .sltu(sltu),
    .\xor (\xor ), .lw(lw), .bgtz(bgtz), .sw(sw), .bltz(bltz), .addi(addi), .andi(andi), .halt(halt),
    .pop(pop), .slti(slti), .ori(ori), .tty(tty), .push(push), .blez(blez), .sltiu(sltiu), .xori(xori),
    .rnd(rnd), .beq(beq), .mfhi(mfhi), .kbd(kbd), .bne(bne), .mflo(mflo), .func_code(func_code), .Rd(Rd),
    .Rt(Rt), .Rs(Rs), .op_code(op_code), .constant(Constant), .jump_dest(jump_dest), .b_constant(b_constant));
  assign TTY_ASCII_Data = CS_LOAD_TTY ? A[6:0] : 7'bz;  // Controlled_Buffer controlled_buffer_1
  Multiplexer #(.width(5), .enable("false")) multiplexer_2 (
    .in0(Rt), .in1({5{1'b1}}), .out(multiplexer_2_out), .sel(CS_RF_DA_SP));
  Multiplexer #(.width(32), .enable("false")) multiplexer_3 (
    .in0(A), .in1(PC_value), .out(multiplexer_3_out), .sel(CS_M_PC_value));
  Multiplexer #(.width(32), .enable("false")) multiplexer_4 (
    .in0(F), .in1(random_val), .out(multiplexer_4_out), .sel(CS_NEW_RANDOM));
  Multiplexer #(.width(5), .enable("false")) multiplexer_5 (
    .in0(Rd), .in1(multiplexer_2_out), .out(multiplexer_5_out), .sel(CS_RF_DA));
  Multiplexer #(.width(32), .enable("false")) multiplexer_6 (
    .in0(F), .in1(multiplexer_3_out),
    .out({multiplexer_6_out[31:20], RAM_Direction, Offset, multiplexer_6_out[1:0]}), .sel(CS_M));
  // Probe on RAM_Direction
  Multiplexer #(.select(2), .width(32), .enable("false")) multiplexer_7 (
    .in0(multiplexer_4_out), .in1(RAM_Lecture), .in2(Lo), .in3(multiplexer_8_out), .out(multiplexer_7_out),
    .sel(CS_RF_DI));
  Multiplexer #(.width(32), .enable("false")) multiplexer_8 (
    .in0(Hi), .in1(KBD_DATA), .out(multiplexer_8_out), .sel(CS_KBD));
  Register_File register_file_1 (
    .Data_input(multiplexer_7_out), .Data_address(multiplexer_5_out), .Read_Write(Read_or_Write),
    .Reset(Reset), .Output_A(A), .Output_B(To_RAM), .Clock(Clock), .Selector_A(multiplexer_9_out),
    .Selector_B(multiplexer_10_out));
  Multiplexer #(.select(2), .width(5), .enable("false")) multiplexer_9 (
    .in0(Rs), .in1(Rt), .in2({5{1'b1}}), .out(multiplexer_9_out), .sel(CS_RF_SA));  // open: in3
  Divider #(.width(32)) divider_1 (
    .a({multiplexer_6_out[31:20], RAM_Direction, Offset, multiplexer_6_out[1:0]}), .b(32'h4),
    .rem(divider_1_rem));  // open: out, upper
  Multiplexer #(.width(5), .enable("false")) multiplexer_10 (
    .in0(Rt), .in1(Rs), .out(multiplexer_10_out), .sel(CS_RF_SB));
  Subtractor #(.width(32)) subtractor_1 (
    .a({multiplexer_6_out[31:20], RAM_Direction, Offset, multiplexer_6_out[1:0]}), .b(divider_1_rem),
    .out(subtractor_1_out));  // open: bin, bout
  // Probe on subtractor_1_out
  Register #(.width(32), .trigger("falling")) u_LO (.D(Alu_Lo), .en(CS_LO_HI), .Q(Lo), .clk(Clock), .clr(Reset));
  Multiplexer #(.select(2), .width(32), .enable("false")) multiplexer_11 (
    .in0(To_RAM), .in1(Constant), .in2(32'h4), .out(multiplexer_11_out), .sel(CS_ALU_SELECT_B));  // open: in3
  ALU alu_1 (.A(A), .B(multiplexer_11_out), .OP(CS_ALU_OP), .Output(F), .LO(Alu_Lo), .HI(Alu_Hi));
  Register #(.width(32), .trigger("falling")) u_HI (.D(Alu_Hi), .en(CS_LO_HI), .Q(Hi), .clk(Clock), .clr(Reset));
  Random #(.width(32), .trigger("falling")) RANDOM (.clk(Clock), .next(CS_NEW_RANDOM), .out(random_val));  // open: clr
  // Probe on random_val

  // Other names for the same wires on the sheet: B[31:0] = To_RAM; clk = Clock; cs_ALU_B[1:0] = CS_ALU_SELECT_B;
  //   cs_r_w_PC = Read_or_Write_PC; rs_t = Reset; rw = Read_or_Write

  // Notes on the sheet:
  //   Control Unit Signals
  //   Entradas
  //   Trabajo con TTY
  //   Trabajo con RAM
  //   Salidas
  //   Pedir Mul/Div
  //   Operaciones Simples
  //   Operaciones Inmediatas
  //   Trabajo con RAM
  //   Operaciones Compuestas
  //   Especiales
  //   Señales de Salto
endmodule

module ALU (
  input  [31:0] A,
  input  [31:0] B,
  input  [3:0] OP,
  output [31:0] Output,
  output [31:0] LO,
  output [31:0] HI
);

  wire comparator_1_lt, comparator_2_lt;
  wire [31:0] \and , div_hi, div_lo, divu_hi, divu_lo, mul_hi, mul_lo, mulu_hi, mulu_lo, \nor , \or , slt,
       sltu, sub, sum, \xor ;

  Adder #(.width(32)) adder_1 (.a(A), .b(B), .out(sum));  // open: cin, cout
  assign \and  = A & B;  // AND_Gate AND, 32 bits wide
  assign \or  = A | B;  // OR_Gate OR, 32 bits wide
  Subtractor #(.width(32)) subtractor_1 (.a(A), .b(B), .out(sub));  // open: bin, bout
  assign \nor  = ~(A | B);  // NOR_Gate NOR, 32 bits wide
  assign \xor  = A ^ B;  // XOR_Gate XOR, 32 bits wide
  Mult mult_1 (.A(A), .B(B), .LO(mul_lo), .HI(mul_hi));
  Multiplier #(.width(32)) multiplier_1 (.a(A), .b(B), .out(mulu_lo), .cout(mulu_hi));  // open: cin
  Comparator #(.width(32)) comparator_1 (.a(A), .b(B), .lt(comparator_1_lt));  // open: gt, eq
  Multiplexer #(.width(32)) multiplexer_1 (
    .in0({32{1'b0}}), .in1(32'h1), .out(slt), .sel(comparator_1_lt));  // open: en
  Div div_1 (.A(A), .B(B), .HI(div_hi), .LO(div_lo));
  Divider #(.width(32)) divider_1 (.a(A), .b(B), .out(divu_lo), .rem(divu_hi));  // open: upper
  Comparator #(.width(32), .mode("unsigned")) comparator_2 (.a(A), .b(B), .lt(comparator_2_lt));  // open: gt, eq
  Multiplexer #(.width(32)) multiplexer_2 (
    .in0({32{1'b0}}), .in1(32'h1), .out(sltu), .sel(comparator_2_lt));  // open: en
  Multiplexer #(.select(3), .width(32)) multiplexer_3 (
    .in0(sum), .in1(sub), .in2(\and ), .in3(\or ), .in4(\nor ), .in5(\xor ), .in6(slt), .in7(sltu),
    .out(Output), .sel(OP[2:0]));  // open: en
  Multiplexer #(.select(2), .width(32)) multiplexer_4 (
    .in0(mul_lo), .in1(mulu_lo), .in2(div_lo), .in3(divu_lo), .out(LO), .sel(OP[1:0]), .en(OP[3]));
  Multiplexer #(.select(2), .width(32)) multiplexer_5 (
    .in0(mul_hi), .in1(mulu_hi), .in2(div_hi), .in3(divu_hi), .out(HI), .sel(OP[1:0]), .en(OP[3]));

  // Other names for the same wires on the sheet: com = OP[3]; op2[1:0] = OP[1:0]; ops[2:0] = OP[2:0]

  // Notes on the sheet:
  //   Suma
  //   Lógicos
  //   Resta
  //   Multiplicación
  //   Multiplicación U
  //   Set last then
  //   División
  //   División U
  //   Set last then U
endmodule

module Instruction_Decoder (
  input  [31:0] Input_from_the_RAM,
  output nop,
  output add,
  output div,
  output \and ,
  output j,
  output jr,
  output sub,
  output divu,
  output \or ,
  output mult,
  output slt,
  output \nor ,
  output mulu,
  output sltu,
  output \xor ,
  output lw,
  output bgtz,
  output sw,
  output bltz,
  output addi,
  output andi,
  output halt,
  output pop,
  output slti,
  output ori,
  output tty,
  output push,
  output blez,
  output sltiu,
  output xori,
  output rnd,
  output beq,
  output mfhi,
  output kbd,
  output bne,
  output mflo,
  output [5:0] func_code,
  output [4:0] Rd,
  output [4:0] Rt,
  output [4:0] Rs,
  output [5:0] op_code,
  output [31:0] constant,
  output [15:0] b_constant,
  output [25:0] jump_dest
);

  wire and_2_out, and_3_out, and_4_out, and_5_out, and_6_out, and_7_out, and_14_out, and_15_out, and_23_out,
       and_24_out, and_27_out, and_28_out, and_29_out, arit_i_w, aritmetica, b, decoder_select_2b_1__0,
       decoder_select_2b_1__2, decoder_select_2b_1__3, decoder_select_2b_3__0, decoder_select_2b_3__2,
       decoder_select_2b_4__1, decoder_select_2b_5__0, decoder_select_2b_5__2, logic_i, not_1_out, not_2_out,
       not_3_out, not_4_out, not_5_out, not_6_out, not_7_out, not_8_out, not_9_out, not_10_out, not_11_out,
       not_12_out, not_13_out, not_14_out, not_15_out, not_16_out, not_17_out, not_18_out, not_19_out,
       not_20_out, not_21_out, not_22_out, not_23_out, not_24_out, not_25_out, not_26_out, not_27_out,
       not_28_out, not_29_out, not_30_out, not_31_out, not_32_out, or_4_out;
  wire [2:0] bitselector_1_out;

  and and_1 (aritmetica, ~Input_from_the_RAM[26], ~Input_from_the_RAM[27], ~Input_from_the_RAM[28], ~Input_from_the_RAM[29], ~Input_from_the_RAM[30], ~Input_from_the_RAM[31]);  // AND_Gate
  not not_1 (not_1_out, Input_from_the_RAM[6]);
  not not_2 (not_2_out, Input_from_the_RAM[7]);
  not not_3 (not_3_out, Input_from_the_RAM[8]);
  not not_4 (not_4_out, Input_from_the_RAM[9]);
  not not_5 (not_5_out, Input_from_the_RAM[10]);
  not not_6 (not_6_out, Input_from_the_RAM[11]);
  not not_7 (not_7_out, Input_from_the_RAM[12]);
  not not_8 (not_8_out, Input_from_the_RAM[13]);
  not not_9 (not_9_out, Input_from_the_RAM[14]);
  not not_10 (not_10_out, Input_from_the_RAM[15]);
  not not_11 (not_11_out, Input_from_the_RAM[16]);
  not not_12 (not_12_out, Input_from_the_RAM[17]);
  not not_13 (not_13_out, Input_from_the_RAM[18]);
  not not_14 (not_14_out, Input_from_the_RAM[19]);
  not not_15 (not_15_out, Input_from_the_RAM[20]);
  not not_16 (not_16_out, Input_from_the_RAM[26]);
  not not_17 (not_17_out, Input_from_the_RAM[27]);
  not not_18 (not_18_out, Input_from_the_RAM[28]);
  not not_19 (not_19_out, Input_from_the_RAM[29]);
  not not_20 (not_20_out, Input_from_the_RAM[30]);
  not not_21 (not_21_out, Input_from_the_RAM[31]);
  and and_2 (and_2_out, not_1_out, not_2_out, not_3_out, not_4_out, not_5_out, not_6_out, not_7_out, not_8_out, not_9_out, not_10_out, not_11_out, not_12_out, not_13_out, not_14_out, not_15_out, not_16_out, not_17_out, not_18_out, not_19_out, not_20_out, not_21_out);
  and and_3 (and_3_out, Input_from_the_RAM[26], Input_from_the_RAM[28], Input_from_the_RAM[29], Input_from_the_RAM[30], Input_from_the_RAM[31]);
  not not_22 (not_22_out, Input_from_the_RAM[21]);
  not not_23 (not_23_out, Input_from_the_RAM[22]);
  not not_24 (not_24_out, Input_from_the_RAM[23]);
  not not_25 (not_25_out, Input_from_the_RAM[24]);
  not not_26 (not_26_out, Input_from_the_RAM[25]);
  not not_27 (not_27_out, Input_from_the_RAM[0]);
  not not_28 (not_28_out, Input_from_the_RAM[1]);
  not not_29 (not_29_out, Input_from_the_RAM[2]);
  not not_30 (not_30_out, Input_from_the_RAM[3]);
  not not_31 (not_31_out, Input_from_the_RAM[4]);
  not not_32 (not_32_out, Input_from_the_RAM[5]);
  and and_4 (and_4_out, aritmetica, Input_from_the_RAM[4]);
  and and_5 (and_5_out, aritmetica, ~Input_from_the_RAM[4]);  // AND_Gate
  and and_6 (and_6_out, not_22_out, not_23_out, not_24_out, not_25_out, not_26_out, not_27_out, not_28_out, not_29_out, not_30_out, not_31_out, not_32_out);
  and and_7 (and_7_out, ~Input_from_the_RAM[0], ~Input_from_the_RAM[1], ~Input_from_the_RAM[2], Input_from_the_RAM[3], ~Input_from_the_RAM[4], ~Input_from_the_RAM[5]);  // AND_Gate
  Decoder_select_2b decoder_select_2b_1 (
    .Enable(and_5_out), .Seleccionador(2'b00), ._0(decoder_select_2b_1__0), ._1(\or ),
    ._2(decoder_select_2b_1__2), ._3(decoder_select_2b_1__3), .\Objeto_de_selección (Input_from_the_RAM[5:0]));
  and and_8 (halt, Input_from_the_RAM[5], and_3_out);
  and and_9 (tty, ~halt, Input_from_the_RAM[0], and_3_out);  // AND_Gate
  and and_10 (rnd, ~halt, Input_from_the_RAM[1], and_3_out);  // AND_Gate
  and and_11 (kbd, ~halt, Input_from_the_RAM[2], and_3_out);  // AND_Gate
  and and_12 (nop, and_6_out, and_2_out);
  and and_13 (jr, and_2_out, and_7_out);
  and and_14 (and_14_out, and_4_out, Input_from_the_RAM[3]);
  and and_15 (and_15_out, ~Input_from_the_RAM[3], and_4_out);  // AND_Gate
  Decoder #(.disabled(0)) decoder_1 (.out0(mfhi), .out1(mflo), .sel(Input_from_the_RAM[1]), .en(and_15_out));
  or or_1 (arit_i_w, addi, slti, sltiu, sw, lw);
  Decoder_select_2b decoder_select_2b_2 (
    .Enable(and_14_out), .Seleccionador(2'b00), ._0(mult), ._1(mulu), ._2(div), ._3(divu),
    .\Objeto_de_selección (Input_from_the_RAM[5:0]));
  Decoder_select_2b decoder_select_2b_3 (
    .Enable(decoder_select_2b_1__0), .Seleccionador(2'b01), ._0(decoder_select_2b_3__0), ._1(\and ),
    ._2(decoder_select_2b_3__2), .\Objeto_de_selección (Input_from_the_RAM[5:0]));  // open: _3
  and and_16 (slt, Input_from_the_RAM[3], decoder_select_2b_1__2);
  and and_17 (sub, ~Input_from_the_RAM[3], decoder_select_2b_1__2);  // AND_Gate
  and and_18 (sltu, Input_from_the_RAM[3], decoder_select_2b_1__3);
  and and_19 (\nor , ~Input_from_the_RAM[3], decoder_select_2b_1__3);  // AND_Gate
  assign constant = arit_i_w ? {{17{Input_from_the_RAM[15]}}, Input_from_the_RAM[14:0]} : 32'bz;  // Controlled_Buffer controlled_buffer_1
  assign constant = logic_i ? {{16{1'b0}}, Input_from_the_RAM[15:0]} : 32'bz;  // Controlled_Buffer controlled_buffer_2
  assign constant = b ? {{15{Input_from_the_RAM[15]}}, Input_from_the_RAM[14:0], 2'b00} : 32'bz;  // Controlled_Buffer controlled_buffer_3
  and and_20 (add, Input_from_the_RAM[5], decoder_select_2b_3__0);
  and and_21 (\xor , decoder_select_2b_3__2, Input_from_the_RAM[5]);
  or or_2 (logic_i, andi, ori, xori);
  and and_22 (j, ~Input_from_the_RAM[26], Input_from_the_RAM[27], ~Input_from_the_RAM[28], ~Input_from_the_RAM[29], ~Input_from_the_RAM[30], ~Input_from_the_RAM[31]);  // AND_Gate
  and and_23 (and_23_out, Input_from_the_RAM[31], Input_from_the_RAM[30], Input_from_the_RAM[29], ~Input_from_the_RAM[28], ~Input_from_the_RAM[27], ~Input_from_the_RAM[26]);  // AND_Gate
  and and_24 (and_24_out, ~Input_from_the_RAM[31], ~Input_from_the_RAM[30], ~Input_from_the_RAM[29]);  // AND_Gate
  BitSelector #(.width(6), .group(3)) bitselector_1 (
    .in(Input_from_the_RAM[31:26]), .out(bitselector_1_out), .sel(1'b1));
  or or_3 (b, bgtz, bltz, blez, beq, bne);
  and and_25 (pop, ~Input_from_the_RAM[0], and_23_out);  // AND_Gate
  and and_26 (push, Input_from_the_RAM[0], and_23_out);
  and and_27 (and_27_out, and_24_out, Input_from_the_RAM[28]);
  or or_4 (or_4_out, and_27_out, and_28_out);
  and and_28 (and_28_out, and_24_out, Input_from_the_RAM[26]);
  and and_29 (and_29_out, bitselector_1_out[0], ~bitselector_1_out[1], ~bitselector_1_out[2]);  // AND_Gate
  and and_30 (lw, Input_from_the_RAM[26], Input_from_the_RAM[27], ~Input_from_the_RAM[28], ~Input_from_the_RAM[29], ~Input_from_the_RAM[30], Input_from_the_RAM[31]);  // AND_Gate
  Decoder_select_2b decoder_select_2b_4 (
    .Enable(or_4_out), .Seleccionador(2'b00), ._0(beq), ._1(decoder_select_2b_4__1), ._2(blez), ._3(bgtz),
    .\Objeto_de_selección (Input_from_the_RAM[31:26]));
  Decoder_select_2b decoder_select_2b_5 (
    .Enable(and_29_out), .Seleccionador(2'b00), ._0(decoder_select_2b_5__0), ._1(ori),
    ._2(decoder_select_2b_5__2), ._3(sltiu), .\Objeto_de_selección (Input_from_the_RAM[31:26]));
  and and_31 (sw, Input_from_the_RAM[26], Input_from_the_RAM[27], ~Input_from_the_RAM[28], Input_from_the_RAM[29], ~Input_from_the_RAM[30], Input_from_the_RAM[31]);  // AND_Gate
  and and_32 (bltz, ~Input_from_the_RAM[28], decoder_select_2b_4__1);  // AND_Gate
  and and_33 (bne, Input_from_the_RAM[28], decoder_select_2b_4__1);
  and and_34 (addi, ~Input_from_the_RAM[28], decoder_select_2b_5__0);  // AND_Gate
  and and_35 (andi, Input_from_the_RAM[28], decoder_select_2b_5__0);
  and and_36 (slti, ~Input_from_the_RAM[28], decoder_select_2b_5__2);  // AND_Gate
  and and_37 (xori, Input_from_the_RAM[28], decoder_select_2b_5__2);

  assign b_constant = Input_from_the_RAM[15:0];
  assign func_code = Input_from_the_RAM[5:0];
  assign jump_dest = Input_from_the_RAM[25:0];
  assign op_code = Input_from_the_RAM[31:26];
  assign Rd = Input_from_the_RAM[15:11];
  assign Rs = Input_from_the_RAM[25:21];
  assign Rt = Input_from_the_RAM[20:16];

  // Other names for the same wires on the sheet: constant_arit_i_w[31:0] = {{17{Input_from_the_RAM[15]}}, Input_from_the_RAM[14:0]};
  //   constant_b[31:2] = {{15{Input_from_the_RAM[15]}}, Input_from_the_RAM[14:0]};
  //   constant_logic_i[15:0] = Input_from_the_RAM[15:0]; constant_read[15:0] = Input_from_the_RAM[15:0];
  //   fc0 = Input_from_the_RAM[0]; Input[31:0] = Input_from_the_RAM; fc1 = Input_from_the_RAM[1];
  //   fc2 = Input_from_the_RAM[2]; fc3 = Input_from_the_RAM[3]; fc4 = Input_from_the_RAM[4];
  //   fc5 = Input_from_the_RAM[5]; x[4:0] = Input_from_the_RAM[10:6]; oc0 = Input_from_the_RAM[26];
  //   oc1 = Input_from_the_RAM[27]; oc2 = Input_from_the_RAM[28]; oc3 = Input_from_the_RAM[29];
  //   oc4 = Input_from_the_RAM[30]; oc5 = Input_from_the_RAM[31]

  // Notes on the sheet:
  //   4
  //   2
  //   5
  //   3
  //   4
  //   5
  //   0
  //   1
  //   2
  //   0
  //   3
  //   1
  //   Señales
  //   Especiales
  //   Valores
  //   Especiales
  //   mult/div
  //   op
  //   Aritméticas y jr,mflo/hi
  //   Definiendo Constante
  //   Jump
  //   Los b--, pop, push
  //   Los i-constantes
  //   lw,sw
endmodule

module Mult (
  input  [31:0] A,
  input  [31:0] B,
  output [31:0] LO,
  output [31:0] HI
);

  wire adder_1_cout, positive;
  wire [31:0] neg_hi, neg_lo, not_1_out, not_2_out, pos_hi, pos_lo;

  xnor xnor_1 (positive, A[31], B[31]);
  Multiplier #(.width(32)) multiplier_1 (.a(A), .b(B), .out(pos_lo), .cout(pos_hi));  // open: cin
  assign not_1_out = ~pos_lo;  // NOT_Gate not_1, 32 bits wide
  assign not_2_out = ~pos_hi;  // NOT_Gate not_2, 32 bits wide
  Adder #(.width(32)) adder_1 (.a(32'h1), .b(not_1_out), .out(neg_lo), .cout(adder_1_cout));  // open: cin
  Adder #(.width(32)) adder_2 (.a({32{1'b0}}), .b(not_2_out), .out(neg_hi), .cin(adder_1_cout));  // open: cout
  Multiplexer #(.width(32)) multiplexer_1 (.in0(neg_lo), .in1(pos_lo), .out(LO), .sel(positive));  // open: en
  Multiplexer #(.width(32)) multiplexer_2 (.in0(neg_hi), .in1(pos_hi), .out(HI), .sel(positive));  // open: en

  // Other names for the same wires on the sheet: minus_A = A[31]; minus_B = B[31]
endmodule

module to_positive (
  input  [31:0] in_1,
  output [31:0] Output
);

  wire n;
  wire [31:0] minus_in;

  Negator #(.width(32)) negator_1 (.in(in_1), .out(minus_in));
  Comparator #(.width(32)) comparator_1 (.a(in_1), .b({32{1'b0}}), .lt(n));  // open: gt, eq
  Multiplexer #(.width(32)) multiplexer_1 (.in0(in_1), .in1(minus_in), .out(Output), .sel(n));  // open: en

  // Other names for the same wires on the sheet: in[31:0] = in_1
endmodule

module Decoder_select_2b (
  input  Enable,
  input  [1:0] Seleccionador,
  input  [5:0] \Objeto_de_selección ,
  output _0,
  output _1,
  output _2,
  output _3
);

  wire [1:0] bitselector_1_out;

  Decoder #(.select(2), .disabled(0)) decoder_1 (
    .out0(_0), .out1(_1), .out2(_2), .out3(_3), .sel(bitselector_1_out), .en(Enable));
  BitSelector #(.width(6), .group(2)) bitselector_1 (
    .in(\Objeto_de_selección ), .out(bitselector_1_out), .sel(Seleccionador));
endmodule

module Register_File (
  input  [31:0] Data_input,
  input  [4:0] Data_address,
  input  Read_Write,
  input  Reset,
  input  Clock,
  input  [4:0] Selector_A,
  input  [4:0] Selector_B,
  output [31:0] Output_A,
  output [31:0] Output_B
);

  wire e0, e1, e2, e3, e4, e5, e6, e7, e8, e9, e10, e11, e12, e13, e14, e15, e16, e17, e18, e19, e20, e21,
       e22, e23, e24, e25, e26, e27, e28, e29, e30, e31, or_1_out;
  wire [31:0] multiplexer_1_out, S0, S1, S2, S3, S4, S5, S6, S7, S8, S9, S10, S11, S12, S13, S14, S15, S16,
       S17, S18, S19, S20, S21, S22, S23, S24, S25, S26, S27, S28, S29, S30, S31;

  // Probe on Data_input
  Multiplexer #(.width(32), .enable("false")) multiplexer_1 (
    .in0(Data_input), .in1(32'h1000), .out(multiplexer_1_out), .sel(Reset));
  Register #(.width(32), .trigger("falling")) R31 (
    .D(multiplexer_1_out), .en(or_1_out), .Q(S31), .clk(Clock));  // open: clr
  or or_1 (or_1_out, Reset, e31);
  Register #(.width(32), .trigger("falling")) R23 (.D(Data_input), .en(e23), .Q(S23), .clk(Clock), .clr(Reset));
  Register #(.width(32), .trigger("falling")) R15 (.D(Data_input), .en(e15), .Q(S15), .clk(Clock), .clr(Reset));
  Register #(.width(32), .trigger("falling")) R7 (.D(Data_input), .en(e7), .Q(S7), .clk(Clock), .clr(Reset));
  // Probe on S31
  Register #(.width(32), .trigger("falling")) R30 (.D(Data_input), .en(e30), .Q(S30), .clk(Clock), .clr(Reset));
  Register #(.width(32), .trigger("falling")) R22 (.D(Data_input), .en(e22), .Q(S22), .clk(Clock), .clr(Reset));
  Register #(.width(32), .trigger("falling")) R14 (.D(Data_input), .en(e14), .Q(S14), .clk(Clock), .clr(Reset));
  Register #(.width(32), .trigger("falling")) R6 (.D(Data_input), .en(e6), .Q(S6), .clk(Clock), .clr(Reset));
  Register #(.width(32), .trigger("falling")) R29 (.D(Data_input), .en(e29), .Q(S29), .clk(Clock), .clr(Reset));
  Register #(.width(32), .trigger("falling")) R21 (.D(Data_input), .en(e21), .Q(S21), .clk(Clock), .clr(Reset));
  Register #(.width(32), .trigger("falling")) R13 (.D(Data_input), .en(e13), .Q(S13), .clk(Clock), .clr(Reset));
  Register #(.width(32), .trigger("falling")) R5 (.D(Data_input), .en(e5), .Q(S5), .clk(Clock), .clr(Reset));
  Register #(.width(32), .trigger("falling")) R28 (.D(Data_input), .en(e28), .Q(S28), .clk(Clock), .clr(Reset));
  Register #(.width(32), .trigger("falling")) R20 (.D(Data_input), .en(e20), .Q(S20), .clk(Clock), .clr(Reset));
  Register #(.width(32), .trigger("falling")) R12 (.D(Data_input), .en(e12), .Q(S12), .clk(Clock), .clr(Reset));
  Register #(.width(32), .trigger("falling")) R4 (.D(Data_input), .en(e4), .Q(S4), .clk(Clock), .clr(Reset));
  Register #(.width(32), .trigger("falling")) R27 (.D(Data_input), .en(e27), .Q(S27), .clk(Clock), .clr(Reset));
  Register #(.width(32), .trigger("falling")) R19 (.D(Data_input), .en(e19), .Q(S19), .clk(Clock), .clr(Reset));
  Register #(.width(32), .trigger("falling")) R11 (.D(Data_input), .en(e11), .Q(S11), .clk(Clock), .clr(Reset));
  Register #(.width(32), .trigger("falling")) R3 (.D(Data_input), .en(e3), .Q(S3), .clk(Clock), .clr(Reset));
  Demultiplexer #(.select(5), .enable("false")) demultiplexer_1 (
    .out0(e0), .out1(e1), .out2(e2), .out3(e3), .out4(e4), .out5(e5), .out6(e6), .out7(e7), .out8(e8),
    .out9(e9), .out10(e10), .out11(e11), .out12(e12), .out13(e13), .out14(e14), .out15(e15), .out16(e16),
    .out17(e17), .out18(e18), .out19(e19), .out20(e20), .out21(e21), .out22(e22), .out23(e23), .out24(e24),
    .out25(e25), .out26(e26), .out27(e27), .out28(e28), .out29(e29), .out30(e30), .out31(e31),
    .in(Read_Write), .sel(Data_address));
  Register #(.width(32), .trigger("falling")) R26 (.D(Data_input), .en(e26), .Q(S26), .clk(Clock), .clr(Reset));
  Register #(.width(32), .trigger("falling")) R18 (.D(Data_input), .en(e18), .Q(S18), .clk(Clock), .clr(Reset));
  Register #(.width(32), .trigger("falling")) R10 (.D(Data_input), .en(e10), .Q(S10), .clk(Clock), .clr(Reset));
  Register #(.width(32), .trigger("falling")) R2 (.D(Data_input), .en(e2), .Q(S2), .clk(Clock), .clr(Reset));
  Register #(.width(32), .trigger("falling")) R25 (.D(Data_input), .en(e25), .Q(S25), .clk(Clock), .clr(Reset));
  Register #(.width(32), .trigger("falling")) R17 (.D(Data_input), .en(e17), .Q(S17), .clk(Clock), .clr(Reset));
  Register #(.width(32), .trigger("falling")) R9 (.D(Data_input), .en(e9), .Q(S9), .clk(Clock), .clr(Reset));
  Register #(.width(32), .trigger("falling")) R1 (.D(Data_input), .en(e1), .Q(S1), .clk(Clock), .clr(Reset));
  Register #(.width(32), .trigger("falling")) R24 (.D(Data_input), .en(e24), .Q(S24), .clk(Clock), .clr(Reset));
  Register #(.width(32), .trigger("falling")) R16 (.D(Data_input), .en(e16), .Q(S16), .clk(Clock), .clr(Reset));
  Register #(.width(32), .trigger("falling")) R8 (.D(Data_input), .en(e8), .Q(S8), .clk(Clock), .clr(Reset));
  Register #(.width(32), .trigger("falling")) R0 (.D({32{1'b0}}), .en(e0), .Q(S0), .clk(Clock), .clr(Reset));
  Multiplexer #(.select(5), .width(32)) multiplexer_2 (
    .in0(S0), .in1(S1), .in2(S2), .in3(S3), .in4(S4), .in5(S5), .in6(S6), .in7(S7), .in8(S8), .in9(S9),
    .in10(S10), .in11(S11), .in12(S12), .in13(S13), .in14(S14), .in15(S15), .in16(S16), .in17(S17),
    .in18(S18), .in19(S19), .in20(S20), .in21(S21), .in22(S22), .in23(S23), .in24(S24), .in25(S25),
    .in26(S26), .in27(S27), .in28(S28), .in29(S29), .in30(S30), .in31(S31), .out(Output_A), .sel(Selector_A));  // open: en
  Multiplexer #(.select(5), .width(32)) multiplexer_3 (
    .in0(S0), .in1(S1), .in2(S2), .in3(S3), .in4(S4), .in5(S5), .in6(S6), .in7(S7), .in8(S8), .in9(S9),
    .in10(S10), .in11(S11), .in12(S12), .in13(S13), .in14(S14), .in15(S15), .in16(S16), .in17(S17),
    .in18(S18), .in19(S19), .in20(S20), .in21(S21), .in22(S22), .in23(S23), .in24(S24), .in25(S25),
    .in26(S26), .in27(S27), .in28(S28), .in29(S29), .in30(S30), .in31(S31), .out(Output_B), .sel(Selector_B));  // open: en

  // Other names for the same wires on the sheet: A[31:0] = Output_A; B[31:0] = Output_B; c = Clock;
  //   D[31:0] = Data_input; DA[4:0] = Data_address; Rst = Reset; rw = Read_Write; SA[4:0] = Selector_A;
  //   SB[4:0] = Selector_B

  // Notes on the sheet:
  //   Registros
  //   Enables
  //   Salidas
  //   Selectores de salida
endmodule

module Branch_Control_Unit (
  input  [31:0] IA,
  input  [15:0] Constante,
  input  [25:0] Jump,
  input  [31:0] Rs,
  input  [31:0] Rt,
  input  beq,
  input  bne,
  input  bgtz,
  input  blez,
  input  bltz,
  input  j,
  input  jr,
  output [31:0] Output
);

  wire and_1_out, and_2_out, and_3_out, and_4_out, and_5_out, beq_t, bgtz_t, blez_t, bltz_t, bne_t,
       comparator_1_gt, comparator_1_lt, comparator_2_eq, or_4_out;
  wire [0:0] or_3_out;
  wire [15:0] Const_4;
  wire [31:0] IA_4, jmp_cond_result, multiplexer_1_out;

  Comparator #(.width(32)) comparator_1 (.a(Rs), .b(Rt), .gt(comparator_1_gt), .eq(beq_t), .lt(comparator_1_lt));
  Comparator #(.width(32)) comparator_2 (.a(Rs), .b({32{1'b0}}), .gt(bgtz_t), .eq(comparator_2_eq), .lt(bltz_t));
  and and_1 (and_1_out, beq, beq_t);
  and and_2 (and_2_out, bne, bne_t);
  and and_3 (and_3_out, bgtz, bgtz_t);
  and and_4 (and_4_out, blez, blez_t);
  and and_5 (and_5_out, bltz, bltz_t);
  or or_1 (bne_t, comparator_1_gt, comparator_1_lt);
  or or_2 (blez_t, comparator_2_eq, bltz_t);
  or or_3 (or_3_out[0], and_1_out, and_2_out, and_3_out, and_4_out, and_5_out);
  Multiplexer #(.select(2), .width(32), .enable("false")) multiplexer_1 (
    .in0(Rs), .in1(jmp_cond_result), .in2({IA[31:28], Jump, 2'b00}), .out(multiplexer_1_out),
    .sel({j, or_3_out[0]}));  // open: in3
  or or_4 (or_4_out, j, or_3_out[0], jr);
  Multiplexer #(.width(32), .enable("false")) multiplexer_2 (
    .in0(IA_4), .in1(multiplexer_1_out), .out(Output), .sel(or_4_out));
  Shifter #(.width(16)) shifter_1 (.in(Constante), .\dist (4'b0010), .out(Const_4));
  Adder #(.width(32)) adder_1 (.a(IA), .b(32'h4), .out(IA_4));  // open: cin, cout
  Adder #(.width(32)) adder_2 (.a({{16{1'b0}}, Const_4}), .b(IA_4), .out(jmp_cond_result));  // open: cin, cout
  // Probe on jmp_cond_result

  // Other names for the same wires on the sheet: beq_f = beq; bgtz_f = bgtz; blez_f = blez; bltz_f = bltz;
  //   bne_f = bne; Const[15:0] = Constante; IA_conc_J[31:2] = {IA[31:28], Jump}

  // Notes on the sheet:
  //   Inputs
  //   Comparators
  //   Defining Conditional Jump
  //   Defining Jump
endmodule

module Control_Unit (
  input  add,
  input  slt,
  input  \and ,
  input  \nor ,
  input  mult,
  input  div,
  input  sub,
  input  sltu,
  input  \or ,
  input  \xor ,
  input  mulu,
  input  divu,
  input  addi,
  input  slti,
  input  ori,
  input  j,
  input  bgtz,
  input  beq,
  input  blez,
  input  andi,
  input  sltiu,
  input  xori,
  input  jr,
  input  bltz,
  input  bne,
  input  nop,
  input  halt,
  input  rnd,
  input  lw,
  input  pop,
  input  tty,
  input  kbd,
  input  sw,
  input  push,
  input  KBD_Avaliable,
  input  mfhi,
  input  Clk,
  input  mflo,
  input  R_W_done,
  input  Circ_Reset,
  output Halt_2,
  output KBD_Enable,
  output TTY_Enable,
  output Reset,
  output [3:0] CS_ALU_OP,
  output CS_RF_DA_SP,
  output CS_R_W,
  output [1:0] CS_RF_DI,
  output [1:0] CS_ALU_SELECT_B,
  output [1:0] CS_RF_SA,
  output CS_RF_DA,
  output CS_RF_SB,
  output CS_M,
  output Read_or_Write_PC,
  output CS_M_PC_value,
  output cs_Load_Instruction,
  output CS_LO_HI,
  output CS_NEW_RANDOM,
  output CS_KBD,
  output CS_LOAD_TTY,
  output RAM_R_W,
  output Chip_Select,
  output Start_R_W
);

  wire cs_Load_Instruction_t, demultiplexer_1_out1, \end , END_q, Halt_t, Halt_waiter, idle, IDLE_q, Jumps,
       Lw_chip_select, Lw_chip_select_1, Lw_RAM_r_w, Lw_start_read, Lw_wait, MFHI_end, MFLO_end, not_2_out,
       OI, op_add, op_and, op_or, op_slt, op_sltu, op_sub, op_xor, or_1_out, or_2_out, or_7_out, or_8_out,
       or_9_out, or_10_out, or_11_out, or_13_out, or_15_out, or_32_out, or_37_out, or_38_out, or_42_out, OS,
       POP_chip_select, POP_chip_select_1, POP_end, Pop_start_read, POP_wait, Push_end, Push_r_w_in_SP,
       Push_RAM_r_w, Push_wait, R_W_state, Reading, Reading_wait, select_4_in_ALU_B,
       select_Constant_in_ALU_B, select_RAM_in_RF_DI, select_SP_in_RF_SA, start, start_Jumps, start_OC,
       start_OI, start_OS, Start_state, Sw_chip_select, Sw_end, Sw_wait, Wait_for_Read_2_q,
       Wait_for_Read_3_q, Wait_for_Read_q, Wait_for_Write_2_q, Wait_for_Write_q, working;
  wire [1:0] multiplexer_2_out, multiplexer_3_out, multiplexer_4_out, multiplexer_25_out;
  wire [3:0] ASM_Selector, multiplexer_1_out, multiplexer_7_out, multiplexer_8_out, multiplexer_9_out,
       multiplexer_10_out, multiplexer_11_out, multiplexer_12_out, multiplexer_13_out, multiplexer_14_out,
       multiplexer_15_out, multiplexer_16_out, multiplexer_17_out, multiplexer_18_out, multiplexer_20_out,
       multiplexer_21_out, multiplexer_22_out, multiplexer_23_out, multiplexer_26_out, multiplexer_27_out,
       multiplexer_28_out, multiplexer_29_out, multiplexer_30_out, multiplexer_31_out;

  Register #(.width(1), .trigger("falling")) u_R_W_State (
    .D(R_W_state), .en(or_1_out), .Q(RAM_R_W), .clk(Clk), .clr(Circ_Reset));
  or or_1 (or_1_out, R_W_state, R_W_done);
  Register #(.width(1), .trigger("falling")) u_Start_State (
    .D(Start_state), .en(or_2_out), .Q(Start_R_W), .clk(Clk), .clr(Circ_Reset));
  or or_2 (or_2_out, Start_state, R_W_done);
  or or_3 (Chip_Select, Lw_chip_select_1, POP_chip_select, CS_RF_SB, cs_Load_Instruction_t, Lw_chip_select, Sw_chip_select, CS_M_PC_value, POP_chip_select_1);
  or or_4 (cs_Load_Instruction, cs_Load_Instruction_t, CS_M_PC_value);
  or or_5 (R_W_state, Push_RAM_r_w, Lw_RAM_r_w);
  or or_6 (Start_state, Lw_RAM_r_w, Push_RAM_r_w, Reading, Lw_start_read, Pop_start_read);
  not not_1 (start, Circ_Reset);
  or or_7 (or_7_out, Read_or_Write_PC, idle);
  not not_2 (not_2_out, start);
  or or_8 (or_8_out, not_2_out, Circ_Reset);
  Demultiplexer #(.enable("false")) demultiplexer_1 (
    .out0(idle), .out1(demultiplexer_1_out1), .in(IDLE_q), .sel(start));
  D_Flip_Flop #(.trigger("falling")) u_IDLE (
    .clk(Clk), .D(or_7_out), .Q(IDLE_q), .preset(or_8_out));  // open: Qn, en, reset
  or or_9 (or_9_out, working, demultiplexer_1_out1);
  Demultiplexer #(.select(4), .enable("false")) demultiplexer_2 (
    .out0(Reading), .out1(OS), .out2(OI), .out3(CS_LO_HI), .out4(Jumps), .out5(Pop_start_read),
    .out6(Push_r_w_in_SP), .out7(Lw_start_read), .out8(Lw_RAM_r_w), .out9(MFHI_end), .out10(MFLO_end),
    .out11(Halt_t), .out12(CS_LOAD_TTY), .out13(CS_NEW_RANDOM), .out14(CS_KBD), .in(or_9_out),
    .sel(multiplexer_1_out));  // open: out15
  Multiplexer #(.width(4), .enable("false")) multiplexer_1 (
    .in0(4'b0000), .in1(ASM_Selector), .out(multiplexer_1_out), .sel(working));
  Multiplexer #(.width(2), .enable("false")) multiplexer_2 (
    .in0(2'b10), .in1(2'b11), .out(multiplexer_2_out), .sel(or_11_out));
  or or_10 (or_10_out, MFHI_end, CS_KBD, MFLO_end);
  or or_11 (or_11_out, MFHI_end, CS_KBD);
  Multiplexer #(.width(2), .enable("false")) multiplexer_3 (
    .in0(2'b01), .in1(2'b10), .out(multiplexer_3_out), .sel(select_SP_in_RF_SA));
  // OR_Gate or_12 is placed but not wired
  Multiplexer #(.width(2), .enable("false")) multiplexer_4 (
    .in0(2'b01), .in1(multiplexer_2_out), .out(multiplexer_4_out), .sel(or_10_out));
  Multiplexer #(.width(2), .enable("false")) multiplexer_5 (
    .in0(2'b00), .in1(multiplexer_4_out), .out(CS_RF_DI), .sel(or_13_out));
  or or_13 (or_13_out, select_RAM_in_RF_DI, MFLO_end, MFHI_end, CS_KBD);
  or or_14 (select_RAM_in_RF_DI, POP_chip_select_1, Lw_chip_select_1);
  Multiplexer #(.width(2), .enable("false")) multiplexer_6 (
    .in0(2'b00), .in1(multiplexer_3_out), .out(CS_RF_SA), .sel(or_15_out));
  or or_15 (or_15_out, 1'b0, select_SP_in_RF_SA);
  or or_16 (select_SP_in_RF_SA, POP_chip_select, POP_end, Push_r_w_in_SP);
  Multiplexer #(.width(4), .enable("false")) multiplexer_7 (
    .in0(4'b0001), .in1(4'b0010), .out(multiplexer_7_out), .sel(start_OI));
  Multiplexer #(.width(4), .enable("false")) multiplexer_8 (
    .in0(multiplexer_7_out), .in1(4'b0011), .out(multiplexer_8_out), .sel(start_OC));
  Multiplexer #(.width(4), .enable("false")) multiplexer_9 (
    .in0(multiplexer_8_out), .in1(4'b0100), .out(multiplexer_9_out), .sel(start_Jumps));
  Multiplexer #(.width(4), .enable("false")) multiplexer_10 (
    .in0(multiplexer_9_out), .in1(4'b0101), .out(multiplexer_10_out), .sel(pop));
  or or_17 (start_OS, \nor , \and , \or , slt, sltu, \xor , add, sub);
  or or_18 (start_Jumps, blez, nop, beq, bne, bgtz, bltz, j, jr);
  D_Flip_Flop #(.trigger("falling")) Halt_state (
    .clk(Clk), .D(Halt_2), .Q(Halt_waiter), .reset(Circ_Reset));  // open: Qn, preset, en
  or or_19 (Halt_2, Halt_t, Halt_waiter);
  Multiplexer #(.width(4), .enable("false")) multiplexer_11 (
    .in0(multiplexer_10_out), .in1(4'b0110), .out(multiplexer_11_out), .sel(push));
  Multiplexer #(.width(4), .enable("false")) multiplexer_12 (
    .in0(multiplexer_11_out), .in1(4'b0111), .out(multiplexer_12_out), .sel(lw));
  Multiplexer #(.width(4), .enable("false")) multiplexer_13 (
    .in0(multiplexer_12_out), .in1(4'b1000), .out(multiplexer_13_out), .sel(sw));
  Multiplexer #(.width(4), .enable("false")) multiplexer_14 (
    .in0(multiplexer_13_out), .in1(4'b1001), .out(multiplexer_14_out), .sel(mfhi));
  or or_20 (start_OI, addi, andi, slti, sltiu, ori, xori);
  or or_21 (CS_RF_DA, CS_RF_DA_SP, Lw_chip_select_1, OI);
  or or_22 (CS_RF_DA_SP, POP_end, Push_r_w_in_SP);
  or or_23 (CS_R_W, OS, OI, POP_chip_select_1, POP_end, CS_KBD, Push_r_w_in_SP, Lw_chip_select_1, MFHI_end, MFLO_end, CS_NEW_RANDOM);
  Multiplexer #(.width(4), .enable("false")) multiplexer_15 (
    .in0(multiplexer_16_out), .in1(4'b1011), .out(multiplexer_15_out), .sel(halt));
  Multiplexer #(.width(4), .enable("false")) multiplexer_16 (
    .in0(multiplexer_14_out), .in1(4'b1010), .out(multiplexer_16_out), .sel(mflo));
  Multiplexer #(.width(4), .enable("false")) multiplexer_17 (
    .in0(multiplexer_15_out), .in1(4'b1100), .out(multiplexer_17_out), .sel(tty));
  or or_24 (start_OC, mult, mulu, div, divu);
  Multiplexer #(.width(4), .enable("false")) multiplexer_18 (
    .in0(multiplexer_17_out), .in1(4'b1101), .out(multiplexer_18_out), .sel(rnd));
  Multiplexer #(.width(4), .enable("false")) multiplexer_19 (
    .in0(multiplexer_18_out), .in1(4'b1110), .out(ASM_Selector), .sel(kbd));
  or or_25 (POP_chip_select, POP_wait, Pop_start_read);
  or or_26 (Lw_chip_select, Lw_start_read, Lw_wait);
  and and_1 (KBD_Enable, CS_KBD, KBD_Avaliable);
  D_Flip_Flop #(.trigger("falling")) Wait_for_Read (
    .clk(Clk), .D(Lw_chip_select), .Q(Wait_for_Read_q));  // open: Qn, preset, en, reset
  Demultiplexer #(.enable("false")) demultiplexer_3 (
    .out0(Lw_wait), .out1(Lw_chip_select_1), .in(Wait_for_Read_q), .sel(R_W_done));
  D_Flip_Flop #(.trigger("falling")) Wait_for_Read_2 (
    .clk(Clk), .D(POP_chip_select), .Q(Wait_for_Read_2_q));  // open: Qn, preset, en, reset
  Demultiplexer #(.enable("false")) demultiplexer_4 (
    .out0(POP_wait), .out1(POP_chip_select_1), .in(Wait_for_Read_2_q), .sel(R_W_done));
  D_Flip_Flop #(.trigger("falling")) Wait_Save_SP (
    .clk(Clk), .D(Push_r_w_in_SP), .Q(Push_RAM_r_w));  // open: Qn, preset, en, reset
  or or_27 (CS_RF_SB, Push_RAM_r_w, Push_wait);
  D_Flip_Flop #(.trigger("falling")) Wait_Save_Rd (
    .clk(Clk), .D(POP_chip_select_1), .Q(POP_end));  // open: Qn, preset, en, reset
  or or_28 (CS_M_PC_value, Reading, Reading_wait);
  Multiplexer #(.width(4), .enable("false")) multiplexer_20 (
    .in0(4'b1011), .in1(4'b1010), .out(multiplexer_20_out), .sel(div));
  Multiplexer #(.width(4), .enable("false")) multiplexer_21 (
    .in0(multiplexer_20_out), .in1(4'b1001), .out(multiplexer_21_out), .sel(mulu));
  or or_29 (op_add, add, POP_end, addi);
  or or_30 (op_slt, slt, slti);
  Multiplexer #(.width(4), .enable("false")) multiplexer_22 (
    .in0(multiplexer_21_out), .in1(4'b1000), .out(multiplexer_22_out), .sel(mult));
  or or_31 (Sw_chip_select, Lw_RAM_r_w, Sw_wait);
  Multiplexer #(.width(4), .enable("false")) multiplexer_23 (
    .in0(multiplexer_22_out), .in1(4'b0111), .out(multiplexer_23_out), .sel(op_sltu));
  Multiplexer #(.width(2), .enable("false")) multiplexer_24 (
    .in0(2'b00), .in1(multiplexer_25_out), .out(CS_ALU_SELECT_B), .sel(or_32_out));
  Multiplexer #(.width(2), .enable("false")) multiplexer_25 (
    .in0(2'b01), .in1(2'b10), .out(multiplexer_25_out), .sel(select_4_in_ALU_B));
  or or_32 (or_32_out, select_Constant_in_ALU_B, select_4_in_ALU_B);
  or or_33 (select_4_in_ALU_B, POP_end, Push_r_w_in_SP);
  D_Flip_Flop #(.trigger("falling")) Wait_for_Read_3 (
    .clk(Clk), .D(CS_M_PC_value), .Q(Wait_for_Read_3_q));  // open: Qn, preset, en, reset
  Demultiplexer #(.enable("false")) demultiplexer_5 (
    .out0(Reading_wait), .out1(cs_Load_Instruction_t), .in(Wait_for_Read_3_q), .sel(R_W_done));
  Multiplexer #(.width(4), .enable("false")) multiplexer_26 (
    .in0(multiplexer_23_out), .in1(4'b0110), .out(multiplexer_26_out), .sel(op_slt));
  Multiplexer #(.width(4), .enable("false")) multiplexer_27 (
    .in0(multiplexer_26_out), .in1(4'b0101), .out(multiplexer_27_out), .sel(op_xor));
  or or_34 (select_Constant_in_ALU_B, OI, Sw_chip_select, Lw_chip_select);
  D_Flip_Flop #(.trigger("falling")) Wait_for_Write (
    .clk(Clk), .D(CS_RF_SB), .Q(Wait_for_Write_q));  // open: Qn, preset, en, reset
  Demultiplexer #(.enable("false")) demultiplexer_6 (
    .out0(Push_wait), .out1(Push_end), .in(Wait_for_Write_q), .sel(R_W_done));
  Multiplexer #(.width(4), .enable("false")) multiplexer_28 (
    .in0(multiplexer_27_out), .in1(4'b0100), .out(multiplexer_28_out), .sel(\nor ));
  Multiplexer #(.width(4), .enable("false")) multiplexer_29 (
    .in0(multiplexer_28_out), .in1(4'b0011), .out(multiplexer_29_out), .sel(op_or));
  D_Flip_Flop #(.trigger("falling")) Wait_for_Write_2 (
    .clk(Clk), .D(Sw_chip_select), .Q(Wait_for_Write_2_q));  // open: Qn, preset, en, reset
  or or_35 (op_sub, sub, Push_r_w_in_SP);
  or or_36 (op_or, \or , ori);
  Multiplexer #(.width(4), .enable("false")) multiplexer_30 (
    .in0(multiplexer_29_out), .in1(4'b0010), .out(multiplexer_30_out), .sel(op_and));
  Multiplexer #(.width(4), .enable("false")) multiplexer_31 (
    .in0(multiplexer_30_out), .in1(4'b0001), .out(multiplexer_31_out), .sel(op_sub));
  Demultiplexer #(.enable("false")) demultiplexer_7 (
    .out0(Sw_wait), .out1(Sw_end), .in(Wait_for_Write_2_q), .sel(R_W_done));
  or or_37 (or_37_out, cs_Load_Instruction_t, working);
  Multiplexer #(.width(4), .enable("false")) multiplexer_32 (
    .in0(multiplexer_31_out), .in1(4'b0000), .out(CS_ALU_OP), .sel(op_add));
  D_Flip_Flop #(.trigger("falling")) u_Working (
    .clk(Clk), .D(or_37_out), .Q(working), .reset(or_38_out));  // open: Qn, preset, en
  or or_38 (or_38_out, Sw_wait, POP_wait, Push_RAM_r_w, Read_or_Write_PC, Push_wait, Lw_wait);
  or or_39 (op_xor, \xor , xori);
  or or_40 (op_and, \and , andi);
  or or_41 (op_sltu, sltu, sltiu);
  or or_42 (or_42_out, \end , OS, OI, CS_LO_HI, Jumps, POP_end, Push_end, Lw_chip_select_1, Sw_end, MFHI_end, MFLO_end, CS_LOAD_TTY, CS_NEW_RANDOM, CS_KBD);
  D_Flip_Flop #(.trigger("falling")) u_END (.clk(Clk), .D(or_42_out), .Q(END_q));  // open: Qn, preset, en, reset
  Demultiplexer #(.enable("false")) demultiplexer_8 (.out0(Read_or_Write_PC), .out1(\end ), .in(END_q), .sel(Halt_2));
  or or_43 (CS_M, CS_M_PC_value, POP_chip_select, CS_RF_SB);

  assign Reset = Circ_Reset;
  assign TTY_Enable = CS_LOAD_TTY;

  // Other names for the same wires on the sheet: cs_ALU_B[1:0] = CS_ALU_SELECT_B;
  //   Reading_chip_select = cs_Load_Instruction_t; Halt_enable = Halt_2; Jumps_end = Jumps;
  //   Lw_select_Constant_in_ALU_B = Lw_chip_select; Lw_end = Lw_chip_select_1; Lw_r_w_in_Rt = Lw_chip_select_1;
  //   Lw_select_RAM_in_RF_DI = Lw_chip_select_1; Lw_select_Rt_in_RF_DA = Lw_chip_select_1; Lw_t = Lw_start_read;
  //   cs_r_w_PC = Read_or_Write_PC; end__idle = Read_or_Write_PC; next_instruction = Read_or_Write_PC; OI_end = OI;
  //   OI_r_w = OI; OI_select_Constant_in_ALU_B = OI; OI_select_Rt_in_RF_DA = OI; op_div = div; op_divu = divu;
  //   op_mult = mult; op_mulu = mulu; op_nor = \nor ; OS_end = OS; OS_r_w = OS; POP_r_w_in_Rd = POP_chip_select_1;
  //   POP_select_RAM_in_RF_DI = POP_chip_select_1; POP_select_A_in_M = POP_chip_select;
  //   POP_select_SP_in_RF_SA = POP_chip_select; POP_r_w_in_SP = POP_end; POP_select_4_in_ALU_B = POP_end;
  //   POP_select_Add_in_ALU_OP = POP_end; POP_select_SP_in_RF_DA = POP_end; POP_select_SP_in_RF_SA_1 = POP_end;
  //   POP_t = Pop_start_read; Push_select_4_in_ALU_B = Push_r_w_in_SP; Push_select_SP_in_RF_DA = Push_r_w_in_SP;
  //   Push_select_SP_in_RF_SA = Push_r_w_in_SP; Push_select_Sub_in_ALU_OP = Push_r_w_in_SP; Push_t = Push_r_w_in_SP;
  //   Push_start_write = Push_RAM_r_w; Random = CS_NEW_RANDOM; Random_end = CS_NEW_RANDOM;
  //   Random_new_random = CS_NEW_RANDOM; Random_r_w_in_Rd = CS_NEW_RANDOM; Reading_start_read = Reading;
  //   OC = CS_LO_HI; OC_end = CS_LO_HI; save_LO_HI = CS_LO_HI; select_1_in_M = CS_M;
  //   select_1_in_RF_DA_value_SP = CS_RF_DA_SP; MFHI_select_HI_in_RF_DI = MFHI_end; MFHI_t = MFHI_end;
  //   MFHI_write = MFHI_end; select_HI_in_RF_DI = MFHI_end; KBD_end = CS_KBD; KBD_r_w_in_Rt = CS_KBD;
  //   KBD_select_kbd_in_RF_DI = CS_KBD; KBD_t = CS_KBD; select_KBD_in_RF_DI = CS_KBD;
  //   MFLO_select_LO_in_RF_DI = MFLO_end; MFLO_t = MFLO_end; MFLO_write = MFLO_end; select_LO_in_RF_DI = MFLO_end;
  //   cs_Load_Instruction_1 = CS_M_PC_value; Reading_chip_select_1 = CS_M_PC_value;
  //   Reading_select_PC_value_in_M = CS_M_PC_value; select_PC_value_in_M = CS_M_PC_value; Push_chip_select = CS_RF_SB;
  //   Push_select_A_in_M = CS_RF_SB; Push_select_Rs_in_RF_SB = CS_RF_SB; Push_select_SP_in_RF_SA_1 = CS_RF_SB;
  //   select_Rs_in_RF_SB = CS_RF_SB; select_Rt_SP_in_RF_DA = CS_RF_DA; start_Halt = halt; start_KBD = kbd;
  //   start_Lw = lw; start_MFHI = mfhi; start_MFLO = mflo; start_POP = pop; start_Push = push; start_Random = rnd;
  //   start_Sw = sw; start_Tty = tty; Sw_select_Constant_in_ALU_B = Sw_chip_select; Sw_start_write = Lw_RAM_r_w;
  //   Sw_t = Lw_RAM_r_w; Tty_end = CS_LOAD_TTY; Tty_print_char = CS_LOAD_TTY; Tty_t = CS_LOAD_TTY;
  //   write_register = CS_R_W

  // Notes on the sheet:
  //   Operaciones Simples
  //   Operaciones Inmediatas
  //   Trabajo con RAM
  //   Pedir Mul/Div
  //   Señales de Control para RAM
  //   SALIDAS
  //   Señales de Control para DP
  //   ENTRADAS
  //   Señales de Control para Waiter
  //   Operaciones Compuestas
  //   Especiales
  //   Reloj
  //   Señales de Salto
  //   Selector de B en RF
  //   Selector de DI en RF
  //   Selector de A en RF
  //   VER QUE PASA
  //   NO SELECCIONO RT EN SA
  //   SELECTORES DEL RF
  //   ASM MFHI
  //   ASM Halt
  //   ASM Operaciones Simples
  //   ASM Operaciones Inmediatas
  //   ASM Operaciones Compuestas
  //   ASM Saltos
  //   Selector de Lectura
  //   SELECTOR DE START DEL ASM
  //   Selector
  //    Zona de Uniones
  //   Selector de KBD en RF DI
  //   Selector de Rt/SP en RF DA
  //   Selector de SP en RF DA
  //   ASM MFLO
  //   ASM Random
  //   ASM KBD
  //   mult
  //   mulu
  //   ASM Lw
  //   ASM Push
  //   ASM TTY
  //   ASM Pop
  //   div
  //   divu
  //   ASM Next Instruction
  //   add
  //   slt
  //   SELECTORES DEL ALU
  //   Selector de B en ALU
  //   Selector de Operaciones
  //   ASM Sw
  //   sub
  //   or
  //   xor
  //   and
  //   sltu
  //   nor
  //   Selector de A/PC_value en M
  //   SELECTOR DEL RANDOM
  //   SELECTOR DE MFLO/MFHI
  //   SELECTORES DE LA OPERACIÓN M
  //   Selector de PC_value en M
  //   SELECTOR DEL PC
  //   SELECTOR DEL TTY
endmodule

module Div (
  input  [31:0] A,
  input  [31:0] B,
  output [31:0] LO,
  output [31:0] HI
);

  wire adder_1_cout, positive;
  wire [31:0] neg_hi, neg_lo, not_1_out, not_2_out, pos_hi, pos_lo;

  xnor xnor_1 (positive, A[31], B[31]);
  Divider #(.width(32)) divider_1 (.a(A), .b(B), .out(pos_lo), .rem(pos_hi));  // open: upper
  assign not_1_out = ~pos_lo;  // NOT_Gate not_1, 32 bits wide
  assign not_2_out = ~pos_hi;  // NOT_Gate not_2, 32 bits wide
  Adder #(.width(32)) adder_1 (.a(32'h1), .b(not_1_out), .out(neg_lo), .cout(adder_1_cout));  // open: cin
  Adder #(.width(32)) adder_2 (.a({32{1'b0}}), .b(not_2_out), .out(neg_hi), .cin(adder_1_cout));  // open: cout
  Multiplexer #(.width(32)) multiplexer_1 (.in0(neg_lo), .in1(pos_lo), .out(LO), .sel(positive));  // open: en
  Multiplexer #(.width(32)) multiplexer_2 (.in0(neg_hi), .in1(pos_hi), .out(HI), .sel(positive));  // open: en

  // Other names for the same wires on the sheet: minus_A = A[31]; minus_B = B[31]
endmodule

module Little_Endian (
  input  [31:0] Input,
  output [31:0] out_2
);


  assign out_2 = {Input[7:0], Input[15:8], Input[23:16], Input[31:24]};

  // Other names for the same wires on the sheet: d[7:0] = Input[31:24]; c[7:0] = Input[23:16]; b[7:0] = Input[15:8];
  //   a[7:0] = Input[7:0]

  // Notes on the sheet:
  //   Little Endian
endmodule

module Waiter (
  input  in_1,
  input  in_2,
  input  [3:0] in_3,
  input  [3:0] in_4,
  input  in_5,
  output Wait_Finish
);

  wire Aux___Wait_Time, demultiplexer_1_out0, demultiplexer_1_out1, demultiplexer_2_out0,
       demultiplexer_3_out0, demultiplexer_3_out1, End_q, IDLE_q, Load_aux__1, or_1_out, or_2_out, Reset,
       While_q;
  wire [3:0] Aux___1, Aux_Value, Wait_Time;

  not not_1 (Reset, in_1);
  D_Flip_Flop IDLE (.clk(in_5), .D(or_1_out), .Q(IDLE_q), .preset(Reset));  // open: Qn, en, reset
  or or_1 (or_1_out, demultiplexer_1_out0, demultiplexer_3_out1);
  Demultiplexer #(.enable("false")) demultiplexer_1 (
    .out0(demultiplexer_1_out0), .out1(demultiplexer_1_out1), .in(IDLE_q), .sel(in_1));
  Register #(.width(4)) register_1 (.D(Aux___1), .en(Load_aux__1), .Q(Aux_Value), .clk(in_5), .clr(Reset));
  // Probe on Aux_Value
  Adder #(.width(4)) adder_1 (.a(Aux_Value), .b(4'b0001), .out(Aux___1));  // open: cin, cout
  Multiplexer #(.width(4), .enable("false")) multiplexer_1 (.in0(in_3), .in1(in_4), .out(Wait_Time), .sel(in_2));
  or or_2 (or_2_out, demultiplexer_1_out1, While_q);
  Demultiplexer #(.enable("false")) demultiplexer_2 (
    .out0(demultiplexer_2_out0), .out1(Load_aux__1), .in(or_2_out), .sel(Aux___Wait_Time));
  or or_3 (Wait_Finish, demultiplexer_3_out0, demultiplexer_2_out0);
  Comparator #(.width(4), .mode("unsigned")) comparator_1 (
    .a(Aux_Value), .b(Wait_Time), .lt(Aux___Wait_Time));  // open: gt, eq
  D_Flip_Flop End (.clk(in_5), .D(Wait_Finish), .Q(End_q));  // open: Qn, preset, en, reset
  D_Flip_Flop While (.clk(in_5), .D(Load_aux__1), .Q(While_q), .reset(Reset));  // open: Qn, preset, en
  Demultiplexer #(.enable("false")) demultiplexer_3 (
    .out0(demultiplexer_3_out0), .out1(demultiplexer_3_out1), .in(End_q), .sel(Reset));

  // Other names for the same wires on the sheet: Clk = in_5; R_W = in_2; Read_Time[3:0] = in_3; Start = in_1;
  //   wait_time_finished = Wait_Finish; Write_Time[3:0] = in_4
endmodule

module RAM_Writer (
  input  [1:0] offset,
  input  [31:0] Input,
  output [31:0] Output,
  output [31:0] Output_2,
  output [31:0] Output_3,
  output [31:0] Output_4,
  output [3:0] Mask
);

  wire [31:0] little_endian_1_out_2;

  Little_Endian little_endian_1 (.Input(Input), .out_2(little_endian_1_out_2));
  Demultiplexer #(.select(2), .width(32), .enable("false")) demultiplexer_1 (
    .out0(Output), .out1(Output_2), .out2(Output_3), .out3(Output_4), .in(little_endian_1_out_2), .sel(offset));
  Multiplexer #(.select(2), .width(4), .enable("false")) multiplexer_1 (
    .in0(4'b0001), .in1(4'b0010), .in2(4'b0100), .in3(4'b1000), .out(Mask), .sel(offset));

  // Notes on the sheet:
  //   RAM Writer
endmodule

module RAM_Reader (
  input  [31:0] RAM_Input_1,
  input  [31:0] RAM_Input_2,
  input  [31:0] RAM_Input_3,
  input  [31:0] RAM_Input_4,
  input  [1:0] offset,
  output [31:0] RAM_Input_Selected
);

  wire [31:0] multiplexer_1_out;

  Multiplexer #(.select(2), .width(32), .enable("false")) multiplexer_1 (
    .in0(RAM_Input_1), .in1(RAM_Input_2), .in2(RAM_Input_3), .in3(RAM_Input_4), .out(multiplexer_1_out),
    .sel(offset));
  Little_Endian little_endian_1 (.Input(multiplexer_1_out), .out_2(RAM_Input_Selected));

  // Notes on the sheet:
  //   RAM Reader
endmodule
